// Logisim project calc_hex.circ as structural Verilog
module main (
);

  wire _0_out, _1_out, _2_out, _3_out, _4_out, _5_out, _6_out, _7_out, _8_out, _9_out, A_out, B_out,
       button_2_out, button_3_out, button_out, C_2_out, C_out, D_out, E_out, F_out;
  wire [3:0] componentes_1_lsb, componentes_1_msb, componentes_1_out_22;

  Button _1 (.out(_1_out));
  Button _0 (.out(_0_out));
  Button A (.out(A_out));
  Button B (.out(B_out));
  COMPONENTES componentes_1 (
    .F(F_out), .E(E_out), .D(D_out), .C(C_out), .B(B_out), .A(A_out), ._9(_9_out), ._8(_8_out), ._7(_7_out),
    ._6(_6_out), ._5(_5_out), ._4(_4_out), ._3(_3_out), ._2(_2_out), ._1(_1_out), ._0(_0_out), .C_2(C_2_out),
    .in_18(button_out), .in_19(button_2_out), .in_20(button_3_out), .LSB(componentes_1_lsb),
    .out_22(componentes_1_out_22), .MSB(componentes_1_msb));
  Button _4 (.out(_4_out));
  Button _5 (.out(_5_out));
  Button _2 (.out(_2_out));
  Button _3 (.out(_3_out));
  Button F (.out(F_out));
  Button C (.out(C_out));
  Button E (.out(E_out));
  Button D (.out(D_out));
  Hex_Digit_Display hex_digit_display_1 (.value(componentes_1_out_22));  // open: dp
  Hex_Digit_Display hex_digit_display_2 (.value(componentes_1_msb));  // open: dp
  Button _7 (.out(_7_out));
  Button _9 (.out(_9_out));
  Button _6 (.out(_6_out));
  Button _8 (.out(_8_out));
  Hex_Digit_Display hex_digit_display_3 (.value(componentes_1_lsb));  // open: dp
  Button button (.out(button_out));
  Button button_2 (.out(button_2_out));
  Button button_3 (.out(button_3_out));
  Button C_2 (.out(C_2_out));
endmodule

module _1_2_Som (
  input  A,
  input  B,
  output out_3,
  output out_4
);

  xor xor_1 (out_3, A, B);
  and and_1 (out_4, A, B);
endmodule

module Som_C (
  input  Vem1,
  input  A,
  input  B,
  output S,
  output Vai1
);

  wire and_1_out, and_2_out, and_3_out, xor_1_out;

  xor xor_1 (xor_1_out, A, Vem1);
  and and_1 (and_1_out, A, Vem1);
  and and_2 (and_2_out, B, Vem1);
  and and_3 (and_3_out, A, B);
  xor xor_2 (S, xor_1_out, B);
  or or_1 (Vai1, and_1_out, and_2_out, and_3_out);
endmodule

// +
module SOMA (
  input  [7:0] A,
  input  [7:0] B,
  output [8:0] out_3
);

  wire n1_2_som_1_out_4, som_c_2_vai1, som_c_3_vai1, som_c_4_vai1, som_c_5_vai1, som_c_6_vai1, som_c_7_vai1;

  Som_C som_c_1 (.A(A[7]), .B(B[7]), .Vai1(out_3[8]), .Vem1(som_c_2_vai1), .S(out_3[7]));
  Som_C som_c_2 (.A(A[6]), .B(B[6]), .Vai1(som_c_2_vai1), .Vem1(som_c_3_vai1), .S(out_3[6]));
  Som_C som_c_3 (.A(A[5]), .B(B[5]), .Vai1(som_c_3_vai1), .Vem1(som_c_4_vai1), .S(out_3[5]));
  Som_C som_c_4 (.A(A[4]), .B(B[4]), .Vai1(som_c_4_vai1), .Vem1(som_c_5_vai1), .S(out_3[4]));
  Som_C som_c_5 (.A(A[3]), .B(B[3]), .Vai1(som_c_5_vai1), .Vem1(som_c_6_vai1), .S(out_3[3]));
  Som_C som_c_6 (.A(A[2]), .B(B[2]), .Vai1(som_c_6_vai1), .Vem1(som_c_7_vai1), .S(out_3[2]));
  Som_C som_c_7 (.A(A[1]), .B(B[1]), .Vai1(som_c_7_vai1), .Vem1(n1_2_som_1_out_4), .S(out_3[1]));
  _1_2_Som u_1_2_som_1 (.A(A[0]), .B(B[0]), .out_4(n1_2_som_1_out_4), .out_3(out_3[0]));
endmodule

// 1/2
module _1_2_Sub (
  input  A,
  input  B,
  output Sub,
  output Vai_1
);

  wire not_1_out;

  not not_1 (not_1_out, A);
  xor xor_1 (Sub, A, B);
  and and_1 (Vai_1, not_1_out, B);
endmodule

module Sub_C (
  input  Vem_1,
  input  A,
  input  B,
  output Sub,
  output Vai_1
);

  wire and_1_out, and_2_out, not_1_out, or_1_out;

  ExactlyOne xor_1 (.out(Sub), .in0(A), .in1(B), .in2(Vem_1));
  or or_1 (or_1_out, B, Vem_1);
  and and_1 (and_1_out, B, Vem_1);
  and and_2 (and_2_out, or_1_out, not_1_out);
  not not_1 (not_1_out, A);
  or or_2 (Vai_1, and_2_out, and_1_out);
endmodule

// -
module \SUBTRAÇÃO  (
  input  [7:0] A,
  input  [7:0] B,
  output [8:0] out_3
);

  wire n1_2_sub_1_vai_1, sub_c_2_vai_1, sub_c_3_vai_1, sub_c_4_vai_1, sub_c_5_vai_1, sub_c_6_vai_1,
       sub_c_7_vai_1;

  Sub_C sub_c_1 (.A(A[7]), .B(B[7]), .Vai_1(out_3[8]), .Vem_1(sub_c_2_vai_1), .Sub(out_3[7]));
  Sub_C sub_c_2 (.A(A[6]), .B(B[6]), .Vai_1(sub_c_2_vai_1), .Vem_1(sub_c_3_vai_1), .Sub(out_3[6]));
  Sub_C sub_c_3 (.A(A[5]), .B(B[5]), .Vai_1(sub_c_3_vai_1), .Vem_1(sub_c_4_vai_1), .Sub(out_3[5]));
  Sub_C sub_c_4 (.A(A[4]), .B(B[4]), .Vai_1(sub_c_4_vai_1), .Vem_1(sub_c_5_vai_1), .Sub(out_3[4]));
  Sub_C sub_c_5 (.A(A[3]), .B(B[3]), .Vai_1(sub_c_5_vai_1), .Vem_1(sub_c_6_vai_1), .Sub(out_3[3]));
  Sub_C sub_c_6 (.A(A[2]), .B(B[2]), .Vai_1(sub_c_6_vai_1), .Vem_1(sub_c_7_vai_1), .Sub(out_3[2]));
  Sub_C sub_c_7 (.A(A[1]), .B(B[1]), .Vai_1(sub_c_7_vai_1), .Vem_1(n1_2_sub_1_vai_1), .Sub(out_3[1]));
  _1_2_Sub u_1_2_sub_1 (.A(A[0]), .B(B[0]), .Sub(out_3[0]), .Vai_1(n1_2_sub_1_vai_1));
endmodule

module Conversor_HX_BIN (
  input  _0,
  input  _1,
  input  _2,
  input  _3,
  input  _4,
  input  _5,
  input  _6,
  input  _7,
  input  _8,
  input  _9,
  input  A,
  input  B,
  input  C,
  input  D,
  input  E,
  input  F,
  output [3:0] out_17
);

  or or_1 (out_17[3], _8, _9, A, B, C, D, E, F);
  or or_2 (out_17[2], _4, _5, _6, _7, C, D, E, F);
  or or_3 (out_17[1], _2, _3, _6, _7, A, B, E, F);
  or or_4 (out_17[0], _1, _3, _5, _7, _9, B, D, F);
endmodule

module DECODER (
);

  wire _0_out, _1_out, _2_out, _3_out, _4_out, _5_out, _6_out, _7_out, _8_out, _9_out, A_out, B_out, C_out,
       coder_hex_7seg_1_sa, coder_hex_7seg_1_sb, coder_hex_7seg_1_sc, coder_hex_7seg_1_sd,
       coder_hex_7seg_1_se, coder_hex_7seg_1_sf, coder_hex_7seg_1_sg, D_out, E_out, F_out;
  wire [3:0] conversor_hx_bin_1_out_17;

  Button _0 (.out(_0_out));
  Button _1 (.out(_1_out));
  Button _4 (.out(_4_out));
  Button _3 (.out(_3_out));
  Button _5 (.out(_5_out));
  Button _2 (.out(_2_out));
  Button _6 (.out(_6_out));
  Button _7 (.out(_7_out));
  Button _9 (.out(_9_out));
  Button _8 (.out(_8_out));
  Button D (.out(D_out));
  Button A (.out(A_out));
  Button C (.out(C_out));
  Button B (.out(B_out));
  Conversor_HX_BIN conversor_hx_bin_1 (
    ._0(_0_out), ._1(_1_out), ._2(_2_out), ._3(_3_out), ._4(_4_out), ._5(_5_out), ._6(_6_out), ._7(_7_out),
    ._8(_8_out), ._9(_9_out), .A(A_out), .B(B_out), .C(C_out), .D(D_out), .E(E_out), .F(F_out),
    .out_17(conversor_hx_bin_1_out_17));
  Button F (.out(F_out));
  Button E (.out(E_out));
  coder_hex_7seg coder_hex_7seg_1 (
    .N(conversor_hx_bin_1_out_17), .sA(coder_hex_7seg_1_sa), .sB(coder_hex_7seg_1_sb),
    .sC(coder_hex_7seg_1_sc), .sD(coder_hex_7seg_1_sd), .sE(coder_hex_7seg_1_se), .sF(coder_hex_7seg_1_sf),
    .sG(coder_hex_7seg_1_sg));
  // Probe on conversor_hx_bin_1_out_17
  _7_Segment_Display u_7_segment_display_1 (
    .g(coder_hex_7seg_1_sg), .f(coder_hex_7seg_1_sf), .a(coder_hex_7seg_1_sa), .b(coder_hex_7seg_1_sb),
    .e(coder_hex_7seg_1_se), .d(coder_hex_7seg_1_sd), .c(coder_hex_7seg_1_sc));  // open: dp
endmodule

module MUX4x1 (
  input  [1:0] in_1,
  input  mem1,
  input  soma,
  input  sub,
  input  mem2,
  output S
);

  wire and_1_out, and_2_out, and_3_out, and_4_out, not_1_out, not_2_out, not_3_out, not_4_out;

  not not_1 (not_1_out, in_1[1]);
  not not_2 (not_2_out, in_1[0]);
  not not_3 (not_3_out, in_1[1]);
  not not_4 (not_4_out, in_1[0]);
  and and_1 (and_1_out, mem1, not_1_out, not_2_out);
  and and_2 (and_2_out, soma, not_3_out, in_1[0]);
  and and_3 (and_3_out, sub, in_1[1], not_4_out);
  and and_4 (and_4_out, mem2, in_1[1], in_1[0]);
  or or_1 (S, and_1_out, and_2_out, and_3_out, and_4_out);
endmodule

module flipflop_RS_Basic (
  input  S,
  input  R,
  output Q,
  output nQ
);

  wire not_1_out, not_2_out;

  not not_1 (not_1_out, S);
  not not_2 (not_2_out, R);
  nand nand_1 (Q, not_1_out, nQ);
  nand nand_2 (nQ, Q, not_2_out);
endmodule

// RS
module flipflop_RS_P_C (
  input  Preset,
  input  SET,
  input  CLOCK,
  input  RESET,
  input  Clear,
  output Q,
  output nQ
);

  wire nand_1_out, nand_2_out;

  nand nand_1 (nand_1_out, SET, CLOCK);
  nand nand_2 (nand_2_out, CLOCK, RESET);
  nand nand_3 (Q, Preset, nand_1_out, nQ);
  nand nand_4 (nQ, Q, nand_2_out, Clear);
endmodule

module flipflop_RS_c_clock (
  input  S,
  input  clock,
  input  R,
  output Q,
  output nQ
);

  wire nand_1_out, nand_2_out;

  nand nand_1 (nand_1_out, S, clock);
  nand nand_2 (nand_2_out, clock, R);
  nand nand_3 (Q, nand_1_out, nQ);
  nand nand_4 (nQ, Q, nand_2_out);
endmodule

module memoria1bit (
  input  Entrada,
  output Valor
);

  wire C_out, CK_out, not_1_out;

  not not_1 (not_1_out, Entrada);
  Button CK (.out(CK_out));
  Button C (.out(C_out));
  flipflop_RS_P_C flipflop_rs_p_c_1 (
    .SET(Entrada), .CLOCK(CK_out), .RESET(not_1_out), .Preset(1'b1), .Clear(C_out), .Q(Valor));  // open: nQ
endmodule

module mux (
  input  [7:0] A,
  input  [1:0] in_2,
  input  [8:0] B,
  input  [8:0] C,
  input  [7:0] D,
  output [8:0] out_6
);

  MUX4x1 mux4x1_1 (.mem1(A[0]), .soma(B[0]), .sub(C[0]), .mem2(D[0]), .in_1(in_2), .S(out_6[0]));
  MUX4x1 mux4x1_2 (.mem1(A[1]), .soma(B[1]), .sub(C[1]), .mem2(D[1]), .in_1(in_2), .S(out_6[1]));
  MUX4x1 mux4x1_3 (.mem1(A[2]), .soma(B[2]), .sub(C[2]), .mem2(D[2]), .in_1(in_2), .S(out_6[2]));
  MUX4x1 mux4x1_4 (.mem1(A[3]), .soma(B[3]), .sub(C[3]), .mem2(D[3]), .in_1(in_2), .S(out_6[3]));
  MUX4x1 mux4x1_5 (.mem1(A[4]), .soma(B[4]), .sub(C[4]), .mem2(D[4]), .in_1(in_2), .S(out_6[4]));
  MUX4x1 mux4x1_6 (.mem1(A[5]), .soma(B[5]), .sub(C[5]), .mem2(D[5]), .in_1(in_2), .S(out_6[5]));
  MUX4x1 mux4x1_7 (.mem1(A[6]), .soma(B[6]), .sub(C[6]), .mem2(D[6]), .in_1(in_2), .S(out_6[6]));
  MUX4x1 mux4x1_8 (.mem1(A[7]), .soma(B[7]), .sub(C[7]), .mem2(D[7]), .in_1(in_2), .S(out_6[7]));
  MUX4x1 mux4x1_9 (.mem1(1'b0), .soma(B[8]), .sub(C[8]), .mem2(1'b0), .in_1(in_2), .S(out_6[8]));
endmodule

// HX-7SEG
module coder_hex_7seg (
  input  [3:0] N,
  output sA,
  output sB,
  output sC,
  output sD,
  output sE,
  output sF,
  output sG
);

  wire and_1_out, and_2_out, and_3_out, and_4_out, and_5_out, and_6_out, and_7_out, and_8_out, and_9_out,
       and_10_out, and_11_out, and_12_out, and_13_out, and_14_out, and_15_out, and_16_out, and_17_out,
       and_18_out, and_19_out, and_20_out, and_21_out, and_22_out, and_23_out, and_24_out, and_25_out,
       and_26_out, and_27_out, and_28_out, and_29_out, and_30_out, and_31_out, and_32_out, and_33_out,
       and_34_out, and_35_out, and_36_out, not_1_out, not_2_out, not_3_out, not_4_out, not_5_out, not_6_out,
       not_7_out, not_8_out, not_9_out, not_10_out, not_11_out, not_12_out, not_13_out, not_14_out,
       not_15_out, not_16_out, not_17_out, not_18_out, not_19_out, not_20_out, not_21_out, not_22_out,
       not_23_out, not_24_out, not_25_out, not_26_out, not_27_out, not_28_out, not_29_out, not_30_out,
       not_31_out, not_32_out, not_33_out, not_34_out, not_35_out, not_36_out, not_37_out, not_38_out,
       not_39_out, not_40_out, not_41_out, not_42_out, not_43_out, not_44_out, not_45_out, not_46_out;

  not not_1 (not_1_out, N[2]);
  not not_2 (not_2_out, N[0]);
  not not_3 (not_3_out, N[3]);
  not not_4 (not_4_out, N[3]);
  not not_5 (not_5_out, N[2]);
  not not_6 (not_6_out, N[1]);
  not not_7 (not_7_out, N[0]);
  not not_8 (not_8_out, N[3]);
  not not_9 (not_9_out, N[2]);
  not not_10 (not_10_out, N[3]);
  not not_11 (not_11_out, N[1]);
  not not_12 (not_12_out, N[0]);
  not not_13 (not_13_out, N[2]);
  not not_14 (not_14_out, N[1]);
  not not_15 (not_15_out, N[2]);
  not not_16 (not_16_out, N[0]);
  not not_17 (not_17_out, N[3]);
  not not_18 (not_18_out, N[1]);
  not not_19 (not_19_out, N[3]);
  not not_20 (not_20_out, N[1]);
  not not_21 (not_21_out, N[3]);
  not not_22 (not_22_out, N[1]);
  not not_23 (not_23_out, N[3]);
  not not_24 (not_24_out, N[2]);
  not not_25 (not_25_out, N[3]);
  not not_26 (not_26_out, N[2]);
  not not_27 (not_27_out, N[0]);
  not not_28 (not_28_out, N[2]);
  not not_29 (not_29_out, N[1]);
  not not_30 (not_30_out, N[0]);
  not not_31 (not_31_out, N[1]);
  not not_32 (not_32_out, N[0]);
  not not_33 (not_33_out, N[2]);
  not not_34 (not_34_out, N[0]);
  not not_35 (not_35_out, N[0]);
  not not_36 (not_36_out, N[1]);
  not not_37 (not_37_out, N[0]);
  not not_38 (not_38_out, N[3]);
  not not_39 (not_39_out, N[1]);
  not not_40 (not_40_out, N[0]);
  not not_41 (not_41_out, N[2]);
  not not_42 (not_42_out, N[2]);
  not not_43 (not_43_out, N[0]);
  not not_44 (not_44_out, N[3]);
  not not_45 (not_45_out, N[1]);
  not not_46 (not_46_out, N[2]);
  and and_1 (and_1_out, not_1_out, not_2_out);
  and and_2 (and_2_out, not_3_out, N[1]);
  and and_3 (and_3_out, not_4_out, N[2], N[0]);
  and and_4 (and_4_out, N[2], N[1]);
  and and_5 (and_5_out, N[3], not_5_out, not_6_out);
  and and_6 (and_6_out, N[3], not_7_out);
  and and_7 (and_7_out, not_8_out, not_9_out);
  and and_8 (and_8_out, not_10_out, not_11_out, not_12_out);
  and and_9 (and_9_out, not_13_out, not_14_out);
  and and_10 (and_10_out, not_15_out, not_16_out);
  and and_11 (and_11_out, not_17_out, N[1], N[0]);
  and and_12 (and_12_out, N[3], not_18_out, N[0]);
  and and_13 (and_13_out, not_19_out, not_20_out);
  and and_14 (and_14_out, not_21_out, N[0]);
  and and_15 (and_15_out, not_22_out, N[0]);
  and and_16 (and_16_out, not_23_out, N[2]);
  and and_17 (and_17_out, N[3], not_24_out);
  and and_18 (and_18_out, not_25_out, not_26_out, not_27_out);
  and and_19 (and_19_out, not_28_out, N[1], N[0]);
  and and_20 (and_20_out, N[2], not_29_out, N[0]);
  and and_21 (and_21_out, N[2], N[1], not_30_out);
  and and_22 (and_22_out, N[3], not_31_out, not_32_out);
  and and_23 (and_23_out, not_33_out, not_34_out);
  and and_24 (and_24_out, N[1], not_35_out);
  and and_25 (and_25_out, N[3], N[1]);
  and and_26 (and_26_out, N[3], N[2]);
  and and_27 (and_27_out, not_36_out, not_37_out);
  and and_28 (and_28_out, not_38_out, N[2], not_39_out);
  and and_29 (and_29_out, N[2], not_40_out);
  and and_30 (and_30_out, N[3], not_41_out);
  and and_31 (and_31_out, N[3], N[1]);
  and and_32 (and_32_out, not_42_out, N[1]);
  and and_33 (and_33_out, N[1], not_43_out);
  and and_34 (and_34_out, not_44_out, N[2], not_45_out);
  and and_35 (and_35_out, N[3], not_46_out);
  and and_36 (and_36_out, N[3], N[0]);
  or or_1 (sA, and_1_out, and_2_out, and_3_out, and_4_out, and_5_out, and_6_out);
  or or_2 (sB, and_7_out, and_8_out, and_9_out, and_10_out, and_11_out, and_12_out);
  or or_3 (sC, and_13_out, and_14_out, and_15_out, and_16_out, and_17_out);
  or or_4 (sD, and_18_out, and_19_out, and_20_out, and_21_out, and_22_out);
  or or_5 (sE, and_23_out, and_24_out, and_25_out, and_26_out);
  or or_6 (sF, and_27_out, and_28_out, and_29_out, and_30_out, and_31_out);
  or or_7 (sG, and_32_out, and_33_out, and_34_out, and_35_out, and_36_out);
endmodule

// JK/MS
module flipflop_JK_m_s_p_c (
  input  PRESET,
  input  J,
  input  CLOCK,
  input  K,
  input  CLEAR,
  output Q,
  output nQ
);

  wire nand_1_out, nand_2_out, nand_3_out, nand_4_out, not_1_out;

  nand nand_1 (nand_1_out, nQ, J, CLOCK);
  nand nand_2 (nand_2_out, CLOCK, K, Q);
  nand nand_3 (nand_3_out, nand_1_out, PRESET, nand_4_out);
  not not_1 (not_1_out, CLOCK);
  nand nand_4 (nand_4_out, nand_3_out, CLEAR, nand_2_out);
  flipflop_RS_P_C flipflop_rs_p_c_1 (
    .SET(nand_3_out), .CLOCK(not_1_out), .RESET(nand_4_out), .Preset(PRESET), .Clear(CLEAR), .Q(Q), .nQ(nQ));
endmodule

// D
module flipflop_D (
  input  PRESET,
  input  D,
  input  CK,
  input  CLEAR,
  output Q,
  output nQ
);

  wire not_1_out;

  not not_1 (not_1_out, D);
  flipflop_JK_m_s_p_c flipflop_jk_m_s_p_c_1 (
    .J(D), .CLOCK(CK), .K(not_1_out), .PRESET(PRESET), .CLEAR(CLEAR), .Q(Q), .nQ(nQ));
endmodule

module MB (
  input  [3:0] IN,
  input  ENABLE,
  input  C,
  output [7:0] out_4
);

  flipflop_D flipflop_d_1 (.D(IN[0]), .CK(ENABLE), .PRESET(1'b1), .CLEAR(C), .Q(out_4[0]));  // open: nQ
  flipflop_D flipflop_d_2 (.D(IN[1]), .CK(ENABLE), .PRESET(1'b1), .CLEAR(C), .Q(out_4[1]));  // open: nQ
  flipflop_D flipflop_d_3 (.D(IN[2]), .CK(ENABLE), .PRESET(1'b1), .CLEAR(C), .Q(out_4[2]));  // open: nQ
  flipflop_D flipflop_d_4 (.D(IN[3]), .CK(ENABLE), .PRESET(1'b1), .CLEAR(C), .Q(out_4[3]));  // open: nQ
  flipflop_D flipflop_d_5 (.D(out_4[0]), .CK(ENABLE), .PRESET(1'b1), .CLEAR(C), .Q(out_4[4]));  // open: nQ
  flipflop_D flipflop_d_6 (.D(out_4[1]), .CK(ENABLE), .PRESET(1'b1), .CLEAR(C), .Q(out_4[5]));  // open: nQ
  flipflop_D flipflop_d_7 (.D(out_4[2]), .CK(ENABLE), .PRESET(1'b1), .CLEAR(C), .Q(out_4[6]));  // open: nQ
  flipflop_D flipflop_d_8 (.D(out_4[3]), .CK(ENABLE), .PRESET(1'b1), .CLEAR(C), .Q(out_4[7]));  // open: nQ
endmodule

// U.C
module UC (
  input  _0,
  input  in_2,
  input  in_3,
  input  in_4,
  input  in_5,
  input  in_6,
  input  in_7,
  input  in_8,
  input  in_9,
  input  in_10,
  input  in_11,
  input  in_12,
  input  in_13,
  input  in_14,
  input  in_15,
  input  F,
  input  C,
  input  in_18,
  input  in_19,
  input  in_20,
  output MB1,
  output Clear,
  output MB2,
  output [1:0] MUX
);

  wire and_1_out, and_2_out, and_3_out, and_4_out, flipflop_d_1_q, flipflop_d_2_q, flipflop_d_3_q, not_2_out,
       not_3_out, not_4_out, not_5_out, not_6_out, not_7_out, or_1_out, or_2_out;

  not not_1 (Clear, C);
  not not_2 (not_2_out, in_19);
  not not_3 (not_3_out, not_4_out);
  not not_4 (not_4_out, in_20);
  not not_5 (not_5_out, in_18);
  not not_6 (not_6_out, not_5_out);
  not not_7 (not_7_out, not_2_out);
  flipflop_D flipflop_d_1 (.D(in_18), .CK(not_6_out), .PRESET(1'b1), .CLEAR(Clear), .Q(flipflop_d_1_q));  // open: nQ
  flipflop_D flipflop_d_2 (.D(in_19), .CK(not_7_out), .PRESET(1'b1), .CLEAR(Clear), .Q(flipflop_d_2_q));  // open: nQ
  flipflop_D flipflop_d_3 (.D(in_20), .CK(not_3_out), .PRESET(1'b1), .CLEAR(Clear), .Q(flipflop_d_3_q));  // open: nQ
  or or_1 (or_1_out, flipflop_d_1_q, flipflop_d_2_q);
  and and_1 (and_1_out, ~flipflop_d_1_q, flipflop_d_2_q);  // AND_Gate
  and and_2 (and_2_out, flipflop_d_1_q, ~flipflop_d_2_q, ~flipflop_d_3_q);  // AND_Gate
  and and_3 (and_3_out, flipflop_d_1_q, ~flipflop_d_2_q);  // AND_Gate
  and and_4 (and_4_out, ~flipflop_d_1_q, flipflop_d_2_q, ~flipflop_d_3_q);  // AND_Gate
  or or_2 (or_2_out, F, in_15, in_14, in_13, in_12, in_11, in_10, in_9, in_8, in_7, in_6, in_5, in_4, in_3, in_2, _0);
  and and_5 (MB2, or_2_out, or_1_out);
  or or_3 (MUX[1], and_1_out, and_2_out);
  or or_4 (MUX[0], and_3_out, and_4_out);
  and and_6 (MB1, or_2_out, ~or_1_out);  // AND_Gate
endmodule

module DISPLAY (
  input  [8:0] N,
  output [3:0] A,
  output [3:0] B,
  output [3:0] C
);


  assign A = N[3:0];
  assign B = N[7:4];
  assign C = {3'b000, N[8]};
endmodule

module COMPONENTES (
  input  F,
  input  E,
  input  D,
  input  C,
  input  B,
  input  A,
  input  _9,
  input  _8,
  input  _7,
  input  _6,
  input  _5,
  input  _4,
  input  _3,
  input  _2,
  input  _1,
  input  _0,
  input  C_2,
  input  in_18,
  input  in_19,
  input  in_20,
  output [3:0] LSB,
  output [3:0] out_22,
  output [3:0] MSB
);

  wire uc_1_clear, uc_1_mb1, uc_1_mb2;
  wire [1:0] uc_1_mux;
  wire [3:0] conversor_hx_bin_1_out_17;
  wire [7:0] mb_1_out_4, mb_2_out_4;
  wire [8:0] mux_1_out_6, soma_1_out_3, \subtração_1_out_3 ;

  UC uc_1 (
    .C(C_2), .in_18(in_18), .in_19(in_19), .in_20(in_20), ._0(_0), .in_2(_1), .in_3(_2), .in_4(_3),
    .in_5(_4), .in_6(_5), .in_7(_6), .in_8(_7), .in_9(_8), .in_10(_9), .in_11(A), .in_12(B), .in_13(C),
    .in_14(D), .in_15(E), .F(F), .MB1(uc_1_mb1), .Clear(uc_1_clear), .MB2(uc_1_mb2), .MUX(uc_1_mux));
  Conversor_HX_BIN conversor_hx_bin_1 (
    ._0(_0), ._1(_1), ._2(_2), ._3(_3), ._4(_4), ._5(_5), ._6(_6), ._7(_7), ._8(_8), ._9(_9), .A(A), .B(B),
    .C(C), .D(D), .E(E), .F(F), .out_17(conversor_hx_bin_1_out_17));
  // Probe on uc_1_mb1
  // Probe on conversor_hx_bin_1_out_17
  MB mb_1 (.IN(conversor_hx_bin_1_out_17), .ENABLE(uc_1_mb1), .C(uc_1_clear), .out_4(mb_1_out_4));
  MB mb_2 (.IN(conversor_hx_bin_1_out_17), .ENABLE(uc_1_mb2), .C(uc_1_clear), .out_4(mb_2_out_4));
  // Probe on uc_1_clear
  // Probe on uc_1_mb2
  SOMA soma_1 (.A(mb_1_out_4), .B(mb_2_out_4), .out_3(soma_1_out_3));
  \SUBTRAÇÃO  \subtração_1  (.B(mb_2_out_4), .A(mb_1_out_4), .out_3(\subtração_1_out_3 ));
  // Probe on mb_2_out_4
  // Probe on \subtração_1_out_3 
  // Probe on mb_1_out_4
  mux mux_1 (
    .A(mb_1_out_4), .B(soma_1_out_3), .C(\subtração_1_out_3 ), .D(mb_2_out_4), .in_2(uc_1_mux),
    .out_6(mux_1_out_6));
  // Probe on soma_1_out_3
  DISPLAY display_1 (.N(mux_1_out_6), .C(MSB), .A(LSB), .B(out_22));
  // Probe on mux_1_out_6
endmodule

module principal (
);

  wire _0_out, _1_out, _2_out, _3_out, _4_out, _5_out, _6_out, _7_out, _8_out, _9_out, A_out, B_out,
       button_2_out, button_3_out, button_out, C_2_out, C_out, D_out, E_out, F_out;
  wire [3:0] componentes_1_lsb, componentes_1_msb, componentes_1_out_22;

  Button _2 (.out(_2_out));
  Button _0 (.out(_0_out));
  Button _1 (.out(_1_out));
  Button C (.out(C_out));
  Button A (.out(A_out));
  Button B (.out(B_out));
  Hex_Digit_Display hex_digit_display_1 (.value(componentes_1_msb));  // open: dp
  COMPONENTES componentes_1 (
    .F(F_out), .E(E_out), .D(D_out), .C(C_out), .B(B_out), .A(A_out), ._9(_9_out), ._8(_8_out), ._7(_7_out),
    ._6(_6_out), ._5(_5_out), ._4(_4_out), ._3(_3_out), ._2(_2_out), ._1(_1_out), ._0(_0_out), .C_2(C_2_out),
    .in_18(button_out), .in_19(button_2_out), .in_20(button_3_out), .LSB(componentes_1_lsb),
    .out_22(componentes_1_out_22), .MSB(componentes_1_msb));
  Button _3 (.out(_3_out));
  Button _6 (.out(_6_out));
  Button _5 (.out(_5_out));
  Button _4 (.out(_4_out));
  Button F (.out(F_out));
  Button E (.out(E_out));
  Button D (.out(D_out));
  Hex_Digit_Display hex_digit_display_2 (.value(componentes_1_out_22));  // open: dp
  Button _9 (.out(_9_out));
  Button _8 (.out(_8_out));
  Button _7 (.out(_7_out));
  Hex_Digit_Display hex_digit_display_3 (.value(componentes_1_lsb));  // open: dp
  Button button (.out(button_out));
  Button button_2 (.out(button_2_out));
  Button button_3 (.out(button_3_out));
  Button C_2 (.out(C_2_out));
endmodule
