// Logisim project storage-3bit.circ as structural Verilog: 1 circuit, main circuit main
module main (
  output [2:0] out_1
);

  wire _0_out, _1_out, _2_out, _3_out, _4_out, _5_out, _6_out, _7_out, C_out, nor_1_out, not_1_out,
       octal_7seg_1_a, octal_7seg_1_b, octal_7seg_1_c, octal_7seg_1_d, octal_7seg_1_e, octal_7seg_1_f,
       octal_7seg_1_g;
  wire [2:0] octal_bin_1_out_9;

  Button _7 (.out(_7_out));
  Button _5 (.out(_5_out));
  Button _6 (.out(_6_out));
  Button _4 (.out(_4_out));
  Button _3 (.out(_3_out));
  Button _2 (.out(_2_out));
  Button _1 (.out(_1_out));
  Button C (.out(C_out));
  Button _0 (.out(_0_out));
  nor nor_1 (nor_1_out, _7_out, _6_out, _5_out, _4_out, _3_out, _2_out, _1_out, _0_out);
  not not_1 (not_1_out, nor_1_out);
  MB_3bit mb_3bit_1 (.Input(octal_bin_1_out_9), .Enable(not_1_out), .Clear(C_out), .Output(out_1));
  Octal_Bin octal_bin_1 (
    ._0(_7_out), ._1(_6_out), ._2(_5_out), ._3(_4_out), ._4(_3_out), ._5(_2_out), ._6(_1_out), ._7(_0_out),
    .out_9(octal_bin_1_out_9));
  Octal_7Seg octal_7seg_1 (
    .In(out_1), .a(octal_7seg_1_a), .b(octal_7seg_1_b), .c(octal_7seg_1_c), .d(octal_7seg_1_d),
    .e(octal_7seg_1_e), .f(octal_7seg_1_f), .g(octal_7seg_1_g));
  _7_Segment_Display u_7_segment_display_1 (
    .g(octal_7seg_1_g), .f(octal_7seg_1_f), .a(octal_7seg_1_a), .b(octal_7seg_1_b), .e(octal_7seg_1_e),
    .d(octal_7seg_1_d), .c(octal_7seg_1_c));  // open: dp
endmodule
