// Logisim project jokenpo.circ as structural Verilog: 5 circuits, main circuit main
module main (
);

  wire C_out, jok_7seg_1_a, jok_7seg_1_b, jok_7seg_1_c, jok_7seg_1_d, jok_7seg_1_e, jok_7seg_1_f,
       jok_7seg_1_g, papel_2_out, papel_out, pedra_2_out, pedra_out, tesoura_2_out, tesoura_out;
  wire [1:0] jokenpo_1_out_3, memoria_1_out_8, memoria_1_out_9;

  Button papel (.out(papel_out));
  Button pedra (.out(pedra_out));
  Button tesoura (.out(tesoura_out));
  jok_7seg jok_7seg_1 (
    .in_1(jokenpo_1_out_3), .a(jok_7seg_1_a), .b(jok_7seg_1_b), .c(jok_7seg_1_c), .d(jok_7seg_1_d),
    .e(jok_7seg_1_e), .f(jok_7seg_1_f), .g(jok_7seg_1_g));
  _7_Segment_Display u_7_segment_display_1 (
    .g(jok_7seg_1_g), .f(jok_7seg_1_f), .a(jok_7seg_1_a), .b(jok_7seg_1_b), .e(jok_7seg_1_e),
    .d(jok_7seg_1_d), .c(jok_7seg_1_c));  // open: dp
  jokenpo jokenpo_1 (.in_1(memoria_1_out_8), .in_2(memoria_1_out_9), .out_3(jokenpo_1_out_3));
  memoria memoria_1 (
    .in_4(papel_out), .in_5(pedra_out), .in_6(tesoura_out), .out_8(memoria_1_out_8), .out_9(memoria_1_out_9),
    .clear(C_out), .in_1(papel_2_out), .in_2(pedra_2_out), .in_3(tesoura_2_out));
  Button C (.out(C_out));
  Button papel_2 (.out(papel_2_out));
  Button pedra_2 (.out(pedra_2_out));
  Button tesoura_2 (.out(tesoura_2_out));

  // Notes on the sheet:
  //   jogador A
  //   jogador B
endmodule

module jok2bin (
  input  papel,
  input  pedra,
  input  tesoura,
  output enable,
  output [1:0] \output 
);

  or or_1 (enable, tesoura, pedra, papel);
  or or_2 (\output [0], papel, tesoura);
  or or_3 (\output [1], pedra, tesoura);
endmodule

// MEM
module memoria (
  input  in_1,
  input  in_2,
  input  in_3,
  input  in_4,
  input  in_5,
  input  in_6,
  input  clear,
  output [1:0] out_8,
  output [1:0] out_9
);

  wire jok2bin_1_enable, jok2bin_2_enable, not_1_out;
  wire [1:0] jok2bin_1_output, jok2bin_2_output;

  jok2bin jok2bin_1 (
    .papel(in_4), .pedra(in_5), .tesoura(in_6), .enable(jok2bin_1_enable), .\output (jok2bin_1_output));
  D d_1 (
    .D(jok2bin_1_output[0]), .Clock(jok2bin_1_enable), .CLEAR(not_1_out), .PRESET(1'b1), .Q(out_8[0]));  // open: nQ
  D d_2 (
    .D(jok2bin_1_output[1]), .Clock(jok2bin_1_enable), .CLEAR(not_1_out), .PRESET(1'b1), .Q(out_8[1]));  // open: nQ
  not not_1 (not_1_out, clear);
  D d_3 (
    .D(jok2bin_2_output[0]), .Clock(jok2bin_2_enable), .CLEAR(not_1_out), .PRESET(1'b1), .Q(out_9[0]));  // open: nQ
  D d_4 (
    .D(jok2bin_2_output[1]), .Clock(jok2bin_2_enable), .CLEAR(not_1_out), .PRESET(1'b1), .Q(out_9[1]));  // open: nQ
  jok2bin jok2bin_2 (
    .papel(in_1), .pedra(in_2), .tesoura(in_3), .enable(jok2bin_2_enable), .\output (jok2bin_2_output));
endmodule

module jokenpo (
  input  [1:0] in_1,
  input  [1:0] in_2,
  output [1:0] out_3
);

  wire and_1_out, and_2_out, and_3_out, and_4_out, and_5_out, and_6_out, and_7_out, and_8_out, and_9_out,
       and_10_out, and_11_out, and_12_out, and_13_out, and_14_out, and_15_out, and_16_out, and_17_out,
       and_18_out, not_1_out, not_2_out, not_3_out, not_4_out, not_5_out, not_6_out, not_7_out, not_8_out,
       or_1_out, or_2_out, or_3_out, or_4_out;

  not not_1 (not_1_out, in_1[1]);
  and and_1 (and_1_out, not_1_out, in_1[0]);
  and and_2 (and_2_out, in_1[1], not_2_out);
  not not_2 (not_2_out, in_1[0]);
  not not_3 (not_3_out, in_2[1]);
  and and_3 (and_3_out, not_3_out, in_2[0]);
  and and_4 (and_4_out, in_1[1], in_2[1]);
  not not_4 (not_4_out, in_2[0]);
  and and_5 (and_5_out, in_1[1], in_1[0]);
  and and_6 (and_6_out, in_1[0], not_5_out);
  not not_5 (not_5_out, in_2[1]);
  not not_6 (not_6_out, in_1[1]);
  and and_7 (and_7_out, not_6_out, in_1[0]);
  and and_8 (and_8_out, in_2[1], not_7_out);
  not not_7 (not_7_out, in_2[0]);
  and and_9 (and_9_out, in_1[1], not_8_out);
  not not_8 (not_8_out, in_1[0]);
  and and_10 (and_10_out, in_1[1], in_1[0]);
  and and_11 (and_11_out, and_1_out, in_2[0]);
  and and_12 (and_12_out, and_2_out, and_3_out);
  and and_13 (and_13_out, and_4_out, not_4_out);
  and and_14 (and_14_out, and_5_out, in_2[1]);
  and and_15 (and_15_out, and_6_out, in_2[0]);
  and and_16 (and_16_out, and_7_out, and_8_out);
  and and_17 (and_17_out, and_9_out, in_2[1]);
  and and_18 (and_18_out, and_10_out, in_2[0]);
  or or_1 (or_1_out, and_11_out, and_12_out);
  or or_2 (or_2_out, and_13_out, and_14_out);
  or or_3 (or_3_out, and_15_out, and_16_out);
  or or_4 (or_4_out, and_17_out, and_18_out);
  or or_5 (out_3[1], or_1_out, or_2_out);
  or or_6 (out_3[0], or_3_out, or_4_out);
endmodule

module jok_7seg (
  input  [1:0] in_1,
  output a,
  output b,
  output c,
  output d,
  output e,
  output f,
  output g
);

  wire not_1_out;

  not not_1 (not_1_out, in_1[1]);
  or or_1 (e, in_1[0], in_1[1]);
  or or_2 (f, in_1[0], in_1[1]);
  and and_1 (b, not_1_out, in_1[0]);
  xor xor_1 (c, in_1[1], in_1[0]);

  assign a = in_1[0];
  assign d = in_1[1];
  assign g = 1'b1;
endmodule
