// Logisim project 4bit-7Seg.circ as structural Verilog: 2 circuits, main circuit main
module main (
  input  [3:0] in_1
);

  wire n4bit_7seg_1_a, n4bit_7seg_1_b, n4bit_7seg_1_b_2, n4bit_7seg_1_c, n4bit_7seg_1_c_2, n4bit_7seg_1_d,
       n4bit_7seg_1_e, n4bit_7seg_1_f, n4bit_7seg_1_g;

  _4bit_7seg u_4bit_7seg_1 (
    .in_1(in_1), .b(n4bit_7seg_1_b), .c(n4bit_7seg_1_c), .a(n4bit_7seg_1_a), .b_2(n4bit_7seg_1_b_2),
    .c_2(n4bit_7seg_1_c_2), .d(n4bit_7seg_1_d), .e(n4bit_7seg_1_e), .f(n4bit_7seg_1_f), .g(n4bit_7seg_1_g));
  _7_Segment_Display u_7_segment_display_1 (.b(n4bit_7seg_1_c), .c(n4bit_7seg_1_b));  // open: g, f, a, e, d, dp
  _7_Segment_Display u_7_segment_display_2 (
    .g(n4bit_7seg_1_g), .f(n4bit_7seg_1_f), .a(n4bit_7seg_1_a), .b(n4bit_7seg_1_b_2), .e(n4bit_7seg_1_e),
    .d(n4bit_7seg_1_d), .c(n4bit_7seg_1_c_2));  // open: dp
endmodule

// 4bit-OCTAL
module _4bit_7seg (
  input  [3:0] in_1,
  output b,
  output c,
  output a,
  output b_2,
  output c_2,
  output d,
  output e,
  output f,
  output g
);

  wire and_1_out, and_2_out, and_3_out, and_4_out, and_5_out, and_6_out, and_7_out, and_8_out, and_9_out,
       not_1_out, not_2_out, not_3_out, not_4_out, or_1_out, or_2_out, or_3_out, or_7_out, xnor_1_out,
       xnor_2_out, xnor_3_out;

  not not_1 (not_1_out, in_1[2]);
  not not_2 (not_2_out, in_1[1]);
  not not_3 (not_3_out, in_1[0]);
  and and_1 (and_1_out, in_1[2], not_2_out);
  or or_1 (or_1_out, in_1[1], not_3_out);
  and and_2 (and_2_out, in_1[1], not_3_out);
  or or_2 (or_2_out, not_2_out, not_3_out);
  and and_3 (and_3_out, in_1[2], not_3_out);
  xnor xnor_1 (xnor_1_out, in_1[2], in_1[0]);
  xnor xnor_2 (xnor_2_out, in_1[1], in_1[0]);
  or or_3 (or_3_out, in_1[2], not_2_out);
  and and_4 (and_4_out, and_1_out, in_1[0]);
  and and_5 (and_5_out, or_1_out, not_1_out);
  and and_6 (and_6_out, not_1_out, not_3_out);
  and and_7 (and_7_out, in_1[1], not_3_out);
  and and_8 (and_8_out, not_2_out, not_3_out);
  and and_9 (and_9_out, or_2_out, in_1[2]);
  xnor xnor_3 (xnor_3_out, in_1[2], in_1[1]);
  not not_4 (not_4_out, xnor_3_out);
  or or_4 (a, xnor_1_out, in_1[1]);
  or or_5 (b_2, xnor_2_out, not_1_out);
  or or_6 (c_2, or_3_out, in_1[0]);
  or or_7 (or_7_out, and_5_out, and_2_out);
  or or_8 (e, and_6_out, and_7_out);
  or or_9 (f, and_8_out, and_9_out);
  or or_10 (g, not_4_out, and_3_out);
  or or_11 (d, and_4_out, or_7_out);

  assign b = in_1[3];
  assign c = in_1[3];
endmodule
