// Logisim project Relogio.circ as structural Verilog: 9 circuits, main circuit Main
module Main (
);

  wire CLEAR_out, clock_1_out, contador_de_0_a_5_1_out_3, contador_de_0_a_5_2_out_3,
       contador_de_0_a_9_1_out_3, contador_de_0_a_9_2_out_3, dezenas_das_horas_1_s, dezenas_das_horas_1_u,
       dezenas_das_horas_1_v, dezenas_das_horas_1_w, dezenas_das_horas_1_x, dezenas_das_horas_1_y,
       dezenas_das_horas_1_z, display_de_0_a_59_1_a, display_de_0_a_59_1_a2, display_de_0_a_59_1_b,
       display_de_0_a_59_1_b2, display_de_0_a_59_1_c, display_de_0_a_59_1_c2, display_de_0_a_59_1_d,
       display_de_0_a_59_1_d2, display_de_0_a_59_1_e, display_de_0_a_59_1_e2, display_de_0_a_59_1_f,
       display_de_0_a_59_1_f2, display_de_0_a_59_1_g, display_de_0_a_59_1_g2, display_de_0_a_59_2_a,
       display_de_0_a_59_2_a2, display_de_0_a_59_2_b, display_de_0_a_59_2_b2, display_de_0_a_59_2_c,
       display_de_0_a_59_2_c2, display_de_0_a_59_2_d, display_de_0_a_59_2_d2, display_de_0_a_59_2_e,
       display_de_0_a_59_2_e2, display_de_0_a_59_2_f, display_de_0_a_59_2_f2, display_de_0_a_59_2_g,
       display_de_0_a_59_2_g2, unidades_das_horas_1_s, unidades_das_horas_1_u, unidades_das_horas_1_v,
       unidades_das_horas_1_w, unidades_das_horas_1_x, unidades_das_horas_1_y, unidades_das_horas_1_z;
  wire [2:0] contador_de_0_a_5_1_out_4, contador_de_0_a_5_2_out_4;
  wire [3:0] contador_de_0_a_9_1_out_4, contador_de_0_a_9_2_out_4;
  wire [4:0] contador_de_24_horas_1_out_3;

  Button CLEAR (.out(CLEAR_out));
  Dezenas_das_Horas dezenas_das_horas_1 (
    .a(contador_de_24_horas_1_out_3[4]), .b(contador_de_24_horas_1_out_3[3]),
    .c(contador_de_24_horas_1_out_3[2]), .d(contador_de_24_horas_1_out_3[1]),
    .e(contador_de_24_horas_1_out_3[0]), .x(dezenas_das_horas_1_x), .y(dezenas_das_horas_1_y),
    .z(dezenas_das_horas_1_z), .u(dezenas_das_horas_1_u), .v(dezenas_das_horas_1_v),
    .w(dezenas_das_horas_1_w), .s(dezenas_das_horas_1_s));
  Contador_de_24_Horas contador_de_24_horas_1 (
    .in_1(contador_de_0_a_5_1_out_3), .in_2(CLEAR_out), .out_3(contador_de_24_horas_1_out_3));
  Unidades_das_Horas unidades_das_horas_1 (
    .a(contador_de_24_horas_1_out_3[4]), .b(contador_de_24_horas_1_out_3[3]),
    .c(contador_de_24_horas_1_out_3[2]), .d(contador_de_24_horas_1_out_3[1]),
    .e(contador_de_24_horas_1_out_3[0]), .x(unidades_das_horas_1_x), .y(unidades_das_horas_1_y),
    .z(unidades_das_horas_1_z), .u(unidades_das_horas_1_u), .v(unidades_das_horas_1_v),
    .w(unidades_das_horas_1_w), .s(unidades_das_horas_1_s));
  _7_Segment_Display u_7_segment_display_1 (
    .g(dezenas_das_horas_1_s), .f(dezenas_das_horas_1_v), .a(dezenas_das_horas_1_w),
    .b(dezenas_das_horas_1_x), .e(dezenas_das_horas_1_u), .d(dezenas_das_horas_1_z), .c(dezenas_das_horas_1_y));  // open: dp
  _7_Segment_Display u_7_segment_display_2 (
    .g(unidades_das_horas_1_s), .f(unidades_das_horas_1_v), .a(unidades_das_horas_1_w),
    .b(unidades_das_horas_1_x), .e(unidades_das_horas_1_u), .d(unidades_das_horas_1_z),
    .c(unidades_das_horas_1_y));  // open: dp
  _7_Segment_Display u_7_segment_display_3 (
    .g(display_de_0_a_59_1_g), .f(display_de_0_a_59_1_e), .a(display_de_0_a_59_1_f),
    .b(display_de_0_a_59_1_a), .e(display_de_0_a_59_1_d), .d(display_de_0_a_59_1_c), .c(display_de_0_a_59_1_b));  // open: dp
  _7_Segment_Display u_7_segment_display_4 (
    .g(display_de_0_a_59_1_g2), .f(display_de_0_a_59_1_e2), .a(display_de_0_a_59_1_f2),
    .b(display_de_0_a_59_1_a2), .e(display_de_0_a_59_1_d2), .d(display_de_0_a_59_1_c2),
    .c(display_de_0_a_59_1_b2));  // open: dp
  Contador_de_0_a_9 contador_de_0_a_9_1 (
    .in_1(contador_de_0_a_5_2_out_3), .in_2(CLEAR_out), .out_3(contador_de_0_a_9_1_out_3),
    .out_4(contador_de_0_a_9_1_out_4));
  Contador_de_0_a_5 contador_de_0_a_5_1 (
    .in_1(contador_de_0_a_9_1_out_3), .in_2(CLEAR_out), .out_3(contador_de_0_a_5_1_out_3),
    .out_4(contador_de_0_a_5_1_out_4));
  _7_Segment_Display u_7_segment_display_5 (
    .g(display_de_0_a_59_2_g2), .f(display_de_0_a_59_2_e2), .a(display_de_0_a_59_2_f2),
    .b(display_de_0_a_59_2_a2), .e(display_de_0_a_59_2_d2), .d(display_de_0_a_59_2_c2),
    .c(display_de_0_a_59_2_b2));  // open: dp
  Display_de_0_a_59 display_de_0_a_59_1 (
    .MSB1(contador_de_0_a_9_1_out_4[3]), .in_2(contador_de_0_a_9_1_out_4[2]),
    .in_3(contador_de_0_a_9_1_out_4[1]), .LSB1(contador_de_0_a_9_1_out_4[0]),
    .MSB2(contador_de_0_a_5_1_out_4[2]), .in_6(contador_de_0_a_5_1_out_4[1]),
    .LSB2(contador_de_0_a_5_1_out_4[0]), .A(display_de_0_a_59_1_a), .B(display_de_0_a_59_1_b),
    .C(display_de_0_a_59_1_c), .D(display_de_0_a_59_1_d), .E(display_de_0_a_59_1_e),
    .F(display_de_0_a_59_1_f), .G(display_de_0_a_59_1_g), .A2(display_de_0_a_59_1_a2),
    .B2(display_de_0_a_59_1_b2), .C2(display_de_0_a_59_1_c2), .D2(display_de_0_a_59_1_d2),
    .E2(display_de_0_a_59_1_e2), .F2(display_de_0_a_59_1_f2), .G2(display_de_0_a_59_1_g2));
  _7_Segment_Display u_7_segment_display_6 (
    .g(display_de_0_a_59_2_g), .f(display_de_0_a_59_2_e), .a(display_de_0_a_59_2_f),
    .b(display_de_0_a_59_2_a), .e(display_de_0_a_59_2_d), .d(display_de_0_a_59_2_c), .c(display_de_0_a_59_2_b));  // open: dp
  Contador_de_0_a_5 contador_de_0_a_5_2 (
    .in_1(contador_de_0_a_9_2_out_3), .in_2(CLEAR_out), .out_3(contador_de_0_a_5_2_out_3),
    .out_4(contador_de_0_a_5_2_out_4));
  Contador_de_0_a_9 contador_de_0_a_9_2 (
    .in_1(clock_1_out), .in_2(CLEAR_out), .out_3(contador_de_0_a_9_2_out_3), .out_4(contador_de_0_a_9_2_out_4));
  Display_de_0_a_59 display_de_0_a_59_2 (
    .MSB1(contador_de_0_a_9_2_out_4[3]), .in_2(contador_de_0_a_9_2_out_4[2]),
    .in_3(contador_de_0_a_9_2_out_4[1]), .LSB1(contador_de_0_a_9_2_out_4[0]),
    .MSB2(contador_de_0_a_5_2_out_4[2]), .in_6(contador_de_0_a_5_2_out_4[1]),
    .LSB2(contador_de_0_a_5_2_out_4[0]), .A(display_de_0_a_59_2_a), .B(display_de_0_a_59_2_b),
    .C(display_de_0_a_59_2_c), .D(display_de_0_a_59_2_d), .E(display_de_0_a_59_2_e),
    .F(display_de_0_a_59_2_f), .G(display_de_0_a_59_2_g), .A2(display_de_0_a_59_2_a2),
    .B2(display_de_0_a_59_2_b2), .C2(display_de_0_a_59_2_c2), .D2(display_de_0_a_59_2_d2),
    .E2(display_de_0_a_59_2_e2), .F2(display_de_0_a_59_2_f2), .G2(display_de_0_a_59_2_g2));
  Clock clock_1 (.out(clock_1_out));
endmodule

module Contador_de_0_a_9 (
  input  in_1,
  input  in_2,
  output out_3,
  output [3:0] out_4
);

  wire and_1_out, not_1_out, or_1_out, t_ff_1_qn, t_ff_2_qn, t_ff_3_qn;

  not not_1 (not_1_out, in_1);
  T_Flip_Flop t_ff_1 (.clk(not_1_out), .T(1'b1), .Q(out_4[0]), .Qn(t_ff_1_qn), .reset(or_1_out));  // open: preset, en
  or or_1 (or_1_out, in_2, and_1_out);
  T_Flip_Flop t_ff_2 (.clk(t_ff_1_qn), .T(1'b1), .Q(out_4[1]), .Qn(t_ff_2_qn), .reset(or_1_out));  // open: preset, en
  T_Flip_Flop t_ff_3 (.clk(t_ff_2_qn), .T(1'b1), .Q(out_4[2]), .Qn(t_ff_3_qn), .reset(or_1_out));  // open: preset, en
  T_Flip_Flop t_ff_4 (.clk(t_ff_3_qn), .T(1'b1), .Q(out_3), .reset(or_1_out));  // open: Qn, preset, en
  and and_1 (and_1_out, ~out_4[0], out_4[1], ~out_4[2], out_3);  // AND_Gate

  assign out_4[3] = out_3;
endmodule

module Contador_de_0_a_5 (
  input  in_1,
  input  in_2,
  output out_3,
  output [2:0] out_4
);

  wire and_1_out, not_1_out, or_1_out, t_ff_1_qn, t_ff_2_qn;

  not not_1 (not_1_out, in_1);
  T_Flip_Flop t_ff_1 (.clk(not_1_out), .T(1'b1), .Q(out_4[0]), .Qn(t_ff_1_qn), .reset(or_1_out));  // open: preset, en
  or or_1 (or_1_out, in_2, and_1_out);
  T_Flip_Flop t_ff_2 (.clk(t_ff_1_qn), .T(1'b1), .Q(out_4[1]), .Qn(t_ff_2_qn), .reset(or_1_out));  // open: preset, en
  T_Flip_Flop t_ff_3 (.clk(t_ff_2_qn), .T(1'b1), .Q(out_3), .reset(or_1_out));  // open: Qn, preset, en
  and and_1 (and_1_out, ~out_4[0], out_4[1], out_3);  // AND_Gate

  assign out_4[2] = out_3;
endmodule

module Display_de_0_a_59 (
  input  MSB1,
  input  in_2,
  input  in_3,
  input  LSB1,
  input  MSB2,
  input  in_6,
  input  LSB2,
  output A,
  output B,
  output C,
  output D,
  output E,
  output F,
  output G,
  output A2,
  output B2,
  output C2,
  output D2,
  output E2,
  output F2,
  output G2
);

  Unidades unidades_1 (.a(MSB1), .b(in_2), .c(in_3), .d(LSB1), .A_2(A), .B_2(B), .C_2(C), .D_2(D), .E(E), .F(F), .G(G));
  Dezenas dezenas_1 (.a(MSB2), .b(in_6), .c(LSB2), .A2(A2), .B2(B2), .C2(C2), .D2(D2), .E2(E2), .F2(F2), .G2(G2));
endmodule

module Unidades (
  input  a,
  input  b,
  input  c,
  input  d,
  output A_2,
  output B_2,
  output C_2,
  output D_2,
  output E,
  output F,
  output G
);

  wire and_1_out, and_2_out, and_3_out, and_4_out, and_5_out, and_6_out, and_7_out, and_8_out, and_9_out,
       and_10_out, and_11_out, and_12_out, and_13_out, and_14_out, and_15_out, and_16_out, not_1_out,
       not_2_out, not_3_out, not_4_out, not_5_out, not_6_out, not_7_out, not_8_out, not_9_out, not_10_out,
       not_11_out, not_12_out, not_13_out, not_14_out, not_15_out, not_16_out, not_17_out, not_18_out,
       not_19_out, not_20_out, not_21_out;

  not not_1 (not_1_out, b);
  not not_2 (not_2_out, c);
  and and_1 (and_1_out, not_2_out, not_3_out);
  not not_3 (not_3_out, d);
  and and_2 (and_2_out, c, d);
  not not_4 (not_4_out, c);
  or or_1 (B_2, not_4_out, d, b);
  not not_5 (not_5_out, b);
  and and_3 (and_3_out, not_5_out, not_6_out);
  not not_6 (not_6_out, d);
  not not_7 (not_7_out, b);
  and and_4 (and_4_out, not_7_out, c);
  and and_5 (and_5_out, c, not_8_out);
  not not_8 (not_8_out, d);
  and and_6 (and_6_out, b, not_9_out, d);
  not not_9 (not_9_out, c);
  not not_10 (not_10_out, b);
  and and_7 (and_7_out, not_10_out, not_11_out);
  not not_11 (not_11_out, d);
  and and_8 (and_8_out, c, not_12_out);
  not not_12 (not_12_out, d);
  not not_13 (not_13_out, c);
  and and_9 (and_9_out, not_13_out, not_14_out);
  not not_14 (not_14_out, d);
  and and_10 (and_10_out, b, not_15_out);
  not not_15 (not_15_out, c);
  and and_11 (and_11_out, b, not_16_out);
  not not_16 (not_16_out, d);
  not not_17 (not_17_out, b);
  and and_12 (and_12_out, not_17_out, not_18_out);
  not not_18 (not_18_out, d);
  and and_13 (and_13_out, b, d);
  not not_19 (not_19_out, b);
  and and_14 (and_14_out, not_19_out, c);
  and and_15 (and_15_out, b, not_20_out);
  not not_20 (not_20_out, c);
  and and_16 (and_16_out, b, not_21_out);
  not not_21 (not_21_out, d);
  or or_2 (A_2, not_1_out, and_1_out, and_2_out);
  or or_3 (C_2, and_3_out, and_4_out, and_5_out, and_6_out, a);
  or or_4 (D_2, and_7_out, and_8_out);
  or or_5 (E, and_9_out, and_10_out, and_11_out, a);
  or or_6 (F, and_12_out, c, and_13_out, a);
  or or_7 (G, and_14_out, and_15_out, and_16_out, a);
endmodule

module Dezenas (
  input  a,
  input  b,
  input  c,
  output A2,
  output B2,
  output C2,
  output D2,
  output E2,
  output F2,
  output G2
);

  wire and_1_out, and_2_out, and_3_out, and_4_out, and_5_out, and_6_out, and_7_out, not_1_out, not_2_out,
       not_3_out, not_4_out, not_5_out, not_6_out, not_7_out, not_8_out, not_9_out, not_10_out, not_11_out,
       not_12_out;

  not not_1 (not_1_out, a);
  not not_2 (not_2_out, c);
  not not_3 (not_3_out, b);
  not not_4 (not_4_out, a);
  not not_5 (not_5_out, c);
  not not_6 (not_6_out, a);
  not not_7 (not_7_out, c);
  not not_8 (not_8_out, c);
  not not_9 (not_9_out, b);
  not not_10 (not_10_out, c);
  not not_11 (not_11_out, a);
  not not_12 (not_12_out, c);
  or or_1 (G2, b, a);
  or or_2 (A2, not_1_out, not_2_out);
  or or_3 (B2, not_3_out, c, a);
  and and_1 (and_1_out, not_4_out, not_5_out);
  and and_2 (and_2_out, a, c);
  and and_3 (and_3_out, not_6_out, not_7_out);
  and and_4 (and_4_out, b, not_8_out);
  and and_5 (and_5_out, not_9_out, not_10_out);
  and and_6 (and_6_out, not_11_out, not_12_out);
  and and_7 (and_7_out, a, c);
  or or_4 (C2, and_1_out, b, and_2_out);
  or or_5 (D2, and_3_out, and_4_out);
  or or_6 (E2, and_5_out, a);
  or or_7 (F2, and_6_out, b, and_7_out);
endmodule

module Contador_de_24_Horas (
  input  in_1,
  input  in_2,
  output [4:0] out_3
);

  wire and_1_out, not_1_out, or_1_out, t_ff_1_qn, t_ff_2_qn, t_ff_3_qn, t_ff_4_qn;

  not not_1 (not_1_out, in_1);
  T_Flip_Flop t_ff_1 (.clk(not_1_out), .T(1'b1), .Q(out_3[0]), .Qn(t_ff_1_qn), .reset(or_1_out));  // open: preset, en
  or or_1 (or_1_out, in_2, and_1_out);
  T_Flip_Flop t_ff_2 (.clk(t_ff_1_qn), .T(1'b1), .Q(out_3[1]), .Qn(t_ff_2_qn), .reset(or_1_out));  // open: preset, en
  T_Flip_Flop t_ff_3 (.clk(t_ff_2_qn), .T(1'b1), .Q(out_3[2]), .Qn(t_ff_3_qn), .reset(or_1_out));  // open: preset, en
  T_Flip_Flop t_ff_4 (.clk(t_ff_3_qn), .T(1'b1), .Q(out_3[3]), .Qn(t_ff_4_qn), .reset(or_1_out));  // open: preset, en
  T_Flip_Flop t_ff_5 (.clk(t_ff_4_qn), .T(1'b1), .Q(out_3[4]), .reset(or_1_out));  // open: Qn, preset, en
  and and_1 (and_1_out, ~out_3[0], ~out_3[1], ~out_3[2], out_3[3], out_3[4]);  // AND_Gate
endmodule

module Unidades_das_Horas (
  input  a,
  input  b,
  input  c,
  input  d,
  input  e,
  output x,
  output y,
  output z,
  output u,
  output v,
  output w,
  output s
);

  wire and_1_out, and_2_out, and_3_out, and_4_out, and_5_out, and_6_out, and_7_out, and_8_out, and_9_out,
       and_10_out, and_11_out, and_12_out, and_13_out, and_14_out, and_15_out, and_16_out, and_17_out,
       and_18_out, and_19_out, and_20_out, and_21_out, and_22_out, and_23_out, and_24_out, and_25_out,
       and_26_out, and_27_out, and_28_out, and_29_out, and_30_out, and_31_out, and_32_out, and_33_out,
       and_34_out, and_35_out, and_36_out, and_37_out, and_38_out, and_39_out, and_40_out, and_41_out,
       and_42_out, and_43_out, not_1_out, not_2_out, not_3_out, not_4_out, not_5_out, not_6_out, not_7_out,
       not_8_out, not_9_out, not_10_out, not_11_out, not_12_out, not_13_out, not_14_out, not_15_out,
       not_16_out, not_17_out, not_18_out, not_19_out, not_20_out, not_21_out, not_22_out, not_23_out,
       not_24_out, not_25_out, not_26_out, not_27_out, not_28_out, not_29_out, not_30_out, not_31_out,
       not_32_out, not_33_out, not_34_out, not_35_out, not_36_out, not_37_out, not_38_out, not_39_out,
       not_40_out, not_41_out, not_42_out, not_43_out, not_44_out, not_45_out, not_46_out, not_47_out,
       not_48_out, not_49_out, not_50_out, not_51_out, not_52_out, not_53_out, not_54_out, not_55_out,
       not_56_out, not_57_out, not_58_out, not_59_out, not_60_out;

  not not_1 (not_1_out, a);
  not not_2 (not_2_out, c);
  not not_3 (not_3_out, a);
  not not_4 (not_4_out, d);
  not not_5 (not_5_out, e);
  not not_6 (not_6_out, c);
  not not_7 (not_7_out, c);
  not not_8 (not_8_out, b);
  not not_9 (not_9_out, a);
  not not_10 (not_10_out, d);
  not not_11 (not_11_out, a);
  not not_12 (not_12_out, e);
  not not_13 (not_13_out, b);
  not not_14 (not_14_out, d);
  not not_15 (not_15_out, a);
  not not_16 (not_16_out, c);
  not not_17 (not_17_out, c);
  not not_18 (not_18_out, c);
  not not_19 (not_19_out, e);
  not not_20 (not_20_out, b);
  not not_21 (not_21_out, c);
  not not_22 (not_22_out, b);
  not not_23 (not_23_out, e);
  not not_24 (not_24_out, a);
  not not_25 (not_25_out, d);
  not not_26 (not_26_out, d);
  not not_27 (not_27_out, e);
  not not_28 (not_28_out, c);
  not not_29 (not_29_out, e);
  not not_30 (not_30_out, b);
  not not_31 (not_31_out, e);
  not not_32 (not_32_out, d);
  not not_33 (not_33_out, e);
  not not_34 (not_34_out, e);
  not not_35 (not_35_out, b);
  not not_36 (not_36_out, d);
  not not_37 (not_37_out, e);
  not not_38 (not_38_out, a);
  not not_39 (not_39_out, b);
  not not_40 (not_40_out, a);
  not not_41 (not_41_out, c);
  not not_42 (not_42_out, d);
  not not_43 (not_43_out, e);
  not not_44 (not_44_out, c);
  not not_45 (not_45_out, c);
  not not_46 (not_46_out, e);
  not not_47 (not_47_out, b);
  not not_48 (not_48_out, a);
  not not_49 (not_49_out, d);
  not not_50 (not_50_out, c);
  not not_51 (not_51_out, e);
  not not_52 (not_52_out, b);
  not not_53 (not_53_out, c);
  not not_54 (not_54_out, b);
  not not_55 (not_55_out, e);
  not not_56 (not_56_out, a);
  not not_57 (not_57_out, d);
  not not_58 (not_58_out, d);
  not not_59 (not_59_out, c);
  not not_60 (not_60_out, e);
  and and_1 (and_1_out, not_1_out, not_2_out);
  and and_2 (and_2_out, not_3_out, not_4_out, not_5_out);
  and and_3 (and_3_out, not_6_out, e);
  and and_4 (and_4_out, not_7_out, d);
  and and_5 (and_5_out, not_8_out, d, e);
  and and_6 (and_6_out, not_9_out, b, not_10_out);
  and and_7 (and_7_out, not_11_out, b, not_12_out);
  and and_8 (and_8_out, a, c);
  and and_9 (and_9_out, not_13_out, not_14_out);
  and and_10 (and_10_out, not_15_out, c, d);
  and and_11 (and_11_out, b, not_16_out);
  and and_12 (and_12_out, a, not_17_out);
  and and_13 (and_13_out, not_18_out, not_19_out);
  and and_14 (and_14_out, not_20_out, not_21_out, d);
  and and_15 (and_15_out, not_22_out, d, not_23_out);
  and and_16 (and_16_out, not_24_out, c, not_25_out, e);
  and and_17 (and_17_out, b, not_26_out);
  and and_18 (and_18_out, b, c, e);
  and and_19 (and_19_out, a, not_27_out);
  and and_20 (and_20_out, a, d);
  and and_21 (and_21_out, not_28_out, not_29_out);
  and and_22 (and_22_out, not_30_out, d, not_31_out);
  and and_23 (and_23_out, b, not_32_out, not_33_out);
  and and_24 (and_24_out, a, not_34_out);
  and and_25 (and_25_out, not_35_out, not_36_out, not_37_out);
  and and_26 (and_26_out, not_38_out, not_39_out, c);
  and and_27 (and_27_out, not_40_out, c, d);
  and and_28 (and_28_out, b, not_41_out, not_42_out);
  and and_29 (and_29_out, b, d, not_43_out);
  and and_30 (and_30_out, a, not_44_out);
  and and_31 (and_31_out, not_45_out, not_46_out);
  and and_32 (and_32_out, not_47_out, d);
  and and_33 (and_33_out, not_48_out, c, e);
  and and_34 (and_34_out, b, not_49_out);
  and and_35 (and_35_out, a, not_50_out);
  and and_36 (and_36_out, a, not_51_out);
  and and_37 (and_37_out, not_52_out, not_53_out, d);
  and and_38 (and_38_out, not_54_out, d, not_55_out);
  and and_39 (and_39_out, not_56_out, c, not_57_out);
  and and_40 (and_40_out, b, not_58_out);
  and and_41 (and_41_out, b, c);
  and and_42 (and_42_out, a, not_59_out, not_60_out);
  and and_43 (and_43_out, a, d);
  or or_1 (x, and_1_out, and_2_out, and_3_out, and_4_out, and_5_out, and_6_out, and_7_out, and_8_out);
  or or_2 (y, and_9_out, e, and_10_out, and_11_out, and_12_out);
  or or_3 (z, and_13_out, and_14_out, and_15_out, and_16_out, and_17_out, and_18_out, and_19_out, and_20_out);
  or or_4 (u, and_21_out, and_22_out, and_23_out, and_24_out);
  or or_5 (v, and_25_out, and_26_out, and_27_out, and_28_out, and_29_out, and_30_out);
  or or_6 (w, and_31_out, and_32_out, and_33_out, and_34_out, and_35_out, and_36_out);
  or or_7 (s, and_37_out, and_38_out, and_39_out, and_40_out, and_41_out, and_42_out, and_43_out);
endmodule

module Dezenas_das_Horas (
  input  a,
  input  b,
  input  c,
  input  d,
  input  e,
  output x,
  output y,
  output z,
  output u,
  output v,
  output w,
  output s
);

  wire and_2_out, and_3_out, and_4_out, and_5_out, and_6_out, and_7_out, and_8_out, and_9_out, and_10_out,
       and_11_out, and_12_out, not_1_out, not_2_out, not_3_out, not_4_out, not_5_out, not_6_out, not_7_out,
       not_8_out, not_9_out, not_10_out, not_11_out, not_12_out, not_13_out, not_14_out, not_15_out,
       not_16_out, not_17_out, not_18_out, not_19_out, not_20_out, not_21_out, not_22_out, not_23_out,
       not_24_out, not_25_out;

  not not_1 (not_1_out, a);
  not not_2 (not_2_out, c);
  not not_3 (not_3_out, a);
  not not_4 (not_4_out, b);
  not not_5 (not_5_out, a);
  not not_6 (not_6_out, c);
  not not_7 (not_7_out, d);
  not not_8 (not_8_out, b);
  not not_9 (not_9_out, a);
  not not_10 (not_10_out, b);
  not not_11 (not_11_out, a);
  not not_12 (not_12_out, c);
  not not_13 (not_13_out, d);
  not not_14 (not_14_out, b);
  not not_15 (not_15_out, a);
  not not_16 (not_16_out, b);
  not not_17 (not_17_out, a);
  not not_18 (not_18_out, c);
  not not_19 (not_19_out, d);
  not not_20 (not_20_out, a);
  not not_21 (not_21_out, b);
  not not_22 (not_22_out, a);
  not not_23 (not_23_out, c);
  not not_24 (not_24_out, d);
  not not_25 (not_25_out, b);
  and and_1 (s, a, c);
  or or_1 (y, not_1_out, not_2_out);
  and and_2 (and_2_out, not_3_out, not_4_out);
  and and_3 (and_3_out, not_5_out, not_6_out, not_7_out);
  and and_4 (and_4_out, not_8_out, c);
  and and_5 (and_5_out, not_9_out, not_10_out);
  and and_6 (and_6_out, not_11_out, not_12_out, not_13_out);
  and and_7 (and_7_out, not_14_out, c);
  and and_8 (and_8_out, not_15_out, not_16_out);
  and and_9 (and_9_out, not_17_out, not_18_out, not_19_out);
  and and_10 (and_10_out, not_20_out, not_21_out);
  and and_11 (and_11_out, not_22_out, not_23_out, not_24_out);
  and and_12 (and_12_out, not_25_out, c);
  or or_2 (z, and_2_out, and_3_out, and_4_out);
  or or_3 (u, and_5_out, and_6_out, and_7_out);
  or or_4 (v, and_8_out, and_9_out);
  or or_5 (w, and_10_out, and_11_out, and_12_out);

  assign x = 1'b1;
endmodule
