// Logisim project urna2oTurno.circ as structural Verilog: 11 circuits, main circuit main
module main (
);

  wire _0_out, _1_out, _2_out, _3_out, _4_out, _5_out, _6_out, _7_out, _8_out, _9_out, B_out, C_out,
       circuitourna_1_fim, dec_bin_withenable_1_enable, n7seg1_1_a, n7seg1_1_b, n7seg1_1_c, n7seg1_1_d,
       n7seg1_1_e, n7seg1_1_f, n7seg1_1_g, n7seg2_1_a, n7seg2_1_b, n7seg2_1_c, n7seg2_1_d, n7seg2_1_e,
       n7seg2_1_f, n7seg2_1_g, n7seg3_1_a, n7seg3_1_b, n7seg3_1_c, n7seg3_1_d, n7seg3_1_e, n7seg3_1_f,
       n7seg3_1_g, n7seg4_1_a, n7seg4_1_b, n7seg4_1_c, n7seg4_1_d, n7seg4_1_e, n7seg4_1_f, n7seg4_1_g,
       n7seg5_1_a, n7seg5_1_b, n7seg5_1_c, n7seg5_1_d, n7seg5_1_e, n7seg5_1_f, n7seg5_1_g, voto_1_branco,
       voto_1_c1, voto_1_c2, voto_1_nulo;
  wire [3:0] dec_bin_withenable_1_binout;
  wire [7:0] circuitourna_1_voto;

  Button _1 (.out(_1_out));
  Button _2 (.out(_2_out));
  Button _0 (.out(_0_out));
  Button _5 (.out(_5_out));
  Button _4 (.out(_4_out));
  Button _6 (.out(_6_out));
  Button B (.out(B_out));
  Button _8 (.out(_8_out));
  Button C (.out(C_out));
  _7_Segment_Display u_7_segment_display_1 (
    .g(n7seg1_1_g), .f(n7seg1_1_f), .a(n7seg1_1_a), .b(n7seg1_1_b), .e(n7seg1_1_e), .d(n7seg1_1_d),
    .c(n7seg1_1_c));  // open: dp
  Button _3 (.out(_3_out));
  Button _7 (.out(_7_out));
  Button _9 (.out(_9_out));
  _7seg1 u_7seg1_1 (
    .candidato1(voto_1_c1), .candidato2(voto_1_c2), .branco(voto_1_branco), .nulo(voto_1_nulo),
    .a(n7seg1_1_a), .b(n7seg1_1_b), .c(n7seg1_1_c), .d(n7seg1_1_d), .e(n7seg1_1_e), .f(n7seg1_1_f),
    .g(n7seg1_1_g));
  _7seg2 u_7seg2_1 (
    .candidato1(voto_1_c1), .candidato2(voto_1_c2), .branco(voto_1_branco), .nulo(voto_1_nulo),
    .a(n7seg2_1_a), .b(n7seg2_1_b), .c(n7seg2_1_c), .d(n7seg2_1_d), .e(n7seg2_1_e), .f(n7seg2_1_f),
    .g(n7seg2_1_g));
  _7_Segment_Display u_7_segment_display_2 (
    .g(n7seg2_1_g), .f(n7seg2_1_f), .a(n7seg2_1_a), .b(n7seg2_1_b), .e(n7seg2_1_e), .d(n7seg2_1_d),
    .c(n7seg2_1_c));  // open: dp
  DEC_BIN_withEnable dec_bin_withenable_1 (
    ._0(_0_out), ._1(_1_out), ._2(_2_out), ._3(_3_out), ._4(_4_out), ._5(_5_out), ._6(_6_out), ._7(_7_out),
    ._8(_8_out), ._9(_9_out), .Enable(dec_bin_withenable_1_enable), .BinOUT(dec_bin_withenable_1_binout));
  CircuitoUrna circuitourna_1 (
    .Branco(B_out), .Enable(dec_bin_withenable_1_enable), .Nr(dec_bin_withenable_1_binout), .Clear(C_out),
    .fim(circuitourna_1_fim), .voto(circuitourna_1_voto));
  _7seg3 u_7seg3_1 (
    .candidato1(voto_1_c1), .candidato2(voto_1_c2), .branco(voto_1_branco), .nulo(voto_1_nulo),
    .a(n7seg3_1_a), .b(n7seg3_1_b), .c(n7seg3_1_c), .d(n7seg3_1_d), .e(n7seg3_1_e), .f(n7seg3_1_f),
    .g(n7seg3_1_g));
  _7_Segment_Display u_7_segment_display_3 (
    .g(n7seg3_1_g), .f(n7seg3_1_f), .a(n7seg3_1_a), .b(n7seg3_1_b), .e(n7seg3_1_e), .d(n7seg3_1_d),
    .c(n7seg3_1_c));  // open: dp
  voto voto_1 (
    .fim(circuitourna_1_fim), .in_2(circuitourna_1_voto), .c1(voto_1_c1), .c2(voto_1_c2),
    .branco(voto_1_branco), .nulo(voto_1_nulo));
  _7_Segment_Display u_7_segment_display_4 (
    .g(n7seg4_1_g), .f(n7seg4_1_f), .a(n7seg4_1_a), .b(n7seg4_1_b), .e(n7seg4_1_e), .d(n7seg4_1_d),
    .c(n7seg4_1_c));  // open: dp
  _7seg4 u_7seg4_1 (
    .candidato1(voto_1_c1), .candidato2(voto_1_c2), .branco(voto_1_branco), .nulo(voto_1_nulo),
    .a(n7seg4_1_a), .b(n7seg4_1_b), .c(n7seg4_1_c), .d(n7seg4_1_d), .e(n7seg4_1_e), .f(n7seg4_1_f),
    .g(n7seg4_1_g));
  _7seg5 u_7seg5_1 (
    .candidato1(voto_1_c1), .candidato2(voto_1_c2), .branco(voto_1_branco), .nulo(voto_1_nulo),
    .a(n7seg5_1_a), .b(n7seg5_1_b), .c(n7seg5_1_c), .d(n7seg5_1_d), .e(n7seg5_1_e), .f(n7seg5_1_f),
    .g(n7seg5_1_g));
  _7_Segment_Display u_7_segment_display_5 (
    .g(n7seg5_1_g), .f(n7seg5_1_f), .a(n7seg5_1_a), .b(n7seg5_1_b), .e(n7seg5_1_e), .d(n7seg5_1_d),
    .c(n7seg5_1_c));  // open: dp

  // Notes on the sheet:
  //   Urna Eletrônica:
  //   Nulo - 1111 1111
  //   C1 - Paula - 73 - 0111 0011
  //   C2 - Paulo - 67 - 0110 0111
  //   Branco - 0000 0000
endmodule

// CircUrna
module CircuitoUrna (
  input  Branco,
  input  Enable,
  input  [3:0] Nr,
  input  Clear,
  output fim,
  output [7:0] voto
);

  wire and_1_out, and_2_out, controle_1_branco_2, controle_1_digitou1, not_1_out, votosvalidos_1_out_2;
  wire [3:0] N1_out_4, N2_out_4;
  wire [7:0] brancoounulo_1_out_3;

  controle controle_1 (
    .branco(Branco), .enable(Enable), .clear(Clear), .fim(fim), .Branco_2(controle_1_branco_2),
    .digitou1(controle_1_digitou1));  // open: digitou2
  and and_1 (and_1_out, Enable, controle_1_digitou1);
  MB_4bit N1 (.Data(Nr), .Enable(and_1_out), .Clear(Clear), .out_4(N1_out_4));
  and and_2 (and_2_out, Enable, ~controle_1_digitou1);  // AND_Gate
  MB_4bit N2 (.Data(Nr), .Enable(and_2_out), .Clear(Clear), .out_4(N2_out_4));
  not not_1 (not_1_out, votosvalidos_1_out_2);
  votosValidos votosvalidos_1 (.in_1({N2_out_4, N1_out_4}), .out_2(votosvalidos_1_out_2));
  brancoOUnulo brancoounulo_1 (.branco(controle_1_branco_2), .nulo(not_1_out), .out_3(brancoounulo_1_out_3));
  Mux_2x1_8bit mux_2x1_8bit_1 (
    .A(brancoounulo_1_out_3), .B({N2_out_4, N1_out_4}), .Seletor(votosvalidos_1_out_2), .out_4(voto));
  // Probe on {N2_out_4, N1_out_4}
endmodule

// válido?
module votosValidos (
  input  [7:0] in_1,
  output out_2
);

  wire C1_paula_out, C2_paulo_out;

  and C1_paula (C1_paula_out, ~in_1[7], in_1[6], in_1[5], in_1[4], ~in_1[3], ~in_1[2], in_1[1], in_1[0]);  // AND_Gate
  and C2_paulo (C2_paulo_out, ~in_1[7], in_1[6], in_1[5], ~in_1[4], ~in_1[3], in_1[2], in_1[1], in_1[0]);  // AND_Gate
  or or_1 (out_2, C1_paula_out, C2_paulo_out);
endmodule

module controle (
  input  branco,
  input  enable,
  input  clear,
  output fim,
  output Branco_2,
  output digitou1,
  output digitou2
);

  wire and_1_out, not_1_out;

  not not_1 (not_1_out, clear);
  D d_1 (.D(1'b1), .Clock(branco), .CLEAR(not_1_out), .PRESET(1'b1), .Q(Branco_2));  // open: nQ
  D d_2 (.D(1'b1), .Clock(enable), .CLEAR(not_1_out), .PRESET(1'b1), .Q(digitou1));  // open: nQ
  D d_3 (.D(digitou1), .Clock(enable), .CLEAR(not_1_out), .PRESET(1'b1), .Q(digitou2));  // open: nQ
  or or_1 (fim, Branco_2, and_1_out);
  and and_1 (and_1_out, digitou1, digitou2);
endmodule

// BvN
module brancoOUnulo (
  input  branco,
  input  nulo,
  output [7:0] out_3
);

  wire and_1_out;

  and and_1 (and_1_out, ~branco, nulo);  // AND_Gate
  Mux_2x1_8bit mux_2x1_8bit_1 (.A({8{1'b0}}), .B({8{1'b1}}), .Seletor(and_1_out), .out_4(out_3));
endmodule

module voto (
  input  fim,
  input  [7:0] in_2,
  output c1,
  output c2,
  output branco,
  output nulo
);

  wire branco_out, C1_out, C2_out, nulo_out;

  and u_C1 (C1_out, in_2[0], in_2[1], ~in_2[2], ~in_2[3], in_2[4], in_2[5], in_2[6], ~in_2[7]);  // AND_Gate
  and u_C2 (C2_out, in_2[0], in_2[1], in_2[2], ~in_2[3], ~in_2[4], in_2[5], in_2[6], ~in_2[7]);  // AND_Gate
  and u_branco (branco_out, ~in_2[0], ~in_2[1], ~in_2[2], ~in_2[3], ~in_2[4], ~in_2[5], ~in_2[6], ~in_2[7]);  // AND_Gate
  and u_nulo (nulo_out, in_2[0], in_2[1], in_2[2], in_2[3], in_2[4], in_2[5], in_2[6], in_2[7]);
  and and_1 (c1, fim, C1_out);
  and and_2 (c2, fim, C2_out);
  and and_3 (branco, fim, branco_out);
  and and_4 (nulo, fim, nulo_out);
endmodule

module _7seg1 (
  input  candidato1,
  input  candidato2,
  input  branco,
  input  nulo,
  output a,
  output b,
  output c,
  output d,
  output e,
  output f,
  output g
);

  or or_1 (a, candidato1, candidato2);
  or or_2 (c, branco, nulo);
  or or_3 (e, nulo, branco, candidato2, candidato1);
  or or_4 (f, branco, candidato2, candidato1);

  assign b = a;
  assign d = branco;
  assign g = e;
endmodule

module _7seg2 (
  input  candidato1,
  input  candidato2,
  input  branco,
  input  nulo,
  output a,
  output b,
  output c,
  output d,
  output e,
  output f,
  output g
);

  or or_1 (a, candidato1, candidato2);
  or or_2 (b, candidato1, candidato2, nulo);
  or or_3 (e, candidato1, candidato2, branco, nulo);
  or or_4 (g, candidato1, candidato2, branco);

  assign c = b;
  assign d = nulo;
  assign f = b;
endmodule

module _7seg3 (
  input  candidato1,
  input  candidato2,
  input  branco,
  input  nulo,
  output a,
  output b,
  output c,
  output d,
  output e,
  output f,
  output g
);

  or or_1 (b, candidato1, candidato2, branco);
  or or_2 (d, candidato1, candidato2, nulo);
  or or_3 (e, candidato1, candidato2, branco, nulo);

  assign a = branco;
  assign c = b;
  assign f = e;
  assign g = branco;
endmodule

module _7seg4 (
  input  candidato1,
  input  candidato2,
  input  branco,
  input  nulo,
  output a,
  output b,
  output c,
  output d,
  output e,
  output f,
  output g
);

  or or_1 (c, branco, nulo);
  or or_2 (d, candidato1, candidato2, nulo);
  or or_3 (e, candidato1, candidato2, branco, nulo);

  assign a = nulo;
  assign b = nulo;
  assign f = d;
  assign g = branco;
endmodule

module _7seg5 (
  input  candidato1,
  input  candidato2,
  input  branco,
  input  nulo,
  output a,
  output b,
  output c,
  output d,
  output e,
  output f,
  output g
);

  or or_1 (a, candidato1, candidato2, branco);
  or or_2 (b, candidato1, candidato2);
  or or_3 (d, candidato2, branco);

  assign c = b;
  assign e = a;
  assign f = a;
  assign g = candidato1;
endmodule
