// Logisim project DEC.circ as structural Verilog: 2 circuits, main circuit DEC-BIN
module DEC_BIN (
  input  _0,
  input  _1,
  input  _2,
  input  _3,
  input  _4,
  input  _5,
  input  _6,
  input  _7,
  input  _8,
  input  _9,
  output [3:0] BinOUT
);

  or or_1 (BinOUT[3], _8, _9);
  or or_2 (BinOUT[2], _4, _5, _6, _7);
  or or_3 (BinOUT[1], _2, _3, _6, _7);
  or or_4 (BinOUT[0], _1, _3, _5, _7, _9);
endmodule

// DEC-BIN-Enable
module DEC_BIN_withEnable (
  input  _0,
  input  _1,
  input  _2,
  input  _3,
  input  _4,
  input  _5,
  input  _6,
  input  _7,
  input  _8,
  input  _9,
  output Enable,
  output [3:0] BinOUT
);

  or or_1 (Enable, _0, _1, _2, _3, _4, _5, _6, _7, _8, _9);
  DEC_BIN dec_bin_1 (
    ._0(_0), ._1(_1), ._2(_2), ._3(_3), ._4(_4), ._5(_5), ._6(_6), ._7(_7), ._8(_8), ._9(_9), .BinOUT(BinOUT));
endmodule
