// Logisim project FLIPFLOP.circ as structural Verilog: 4 circuits, main circuit Flip-Flop RS
// RS
module Flip_Flop_RS (
  input  Preset,
  input  SET,
  input  CLOCK,
  input  RESET,
  input  Clear,
  output Q,
  output nQ
);

  wire nand_1_out, nand_2_out;

  nand nand_1 (nand_1_out, SET, CLOCK);
  nand nand_2 (nand_2_out, CLOCK, RESET);
  nand nand_3 (Q, Preset, nand_1_out, nQ);
  nand nand_4 (nQ, Q, nand_2_out, Clear);
endmodule

module JK (
  input  PRESET,
  input  J,
  input  CLOCK,
  input  K,
  input  CLEAR,
  output Q,
  output nQ
);

  wire nand_1_out, nand_2_out, nand_3_out, nand_4_out, not_1_out;

  nand nand_1 (nand_1_out, nQ, J, CLOCK);
  nand nand_2 (nand_2_out, CLOCK, K, Q);
  nand nand_3 (nand_3_out, nand_1_out, PRESET, nand_4_out);
  nand nand_4 (nand_4_out, nand_3_out, CLEAR, nand_2_out);
  Flip_Flop_RS ff_rs_1 (
    .SET(nand_3_out), .CLOCK(not_1_out), .RESET(nand_4_out), .Preset(PRESET), .Clear(CLEAR), .Q(Q), .nQ(nQ));
  not not_1 (not_1_out, CLOCK);
endmodule

module D (
  input  PRESET,
  input  D,
  input  Clock,
  input  CLEAR,
  output Q,
  output nQ
);

  wire not_1_out;

  not not_1 (not_1_out, D);
  JK jk_1 (.J(D), .CLOCK(Clock), .K(not_1_out), .PRESET(PRESET), .CLEAR(CLEAR), .Q(Q), .nQ(nQ));
endmodule

module Flip_Flop_T (
  input  PRESET,
  input  T,
  input  CLOCK,
  input  CLEAR,
  output Q,
  output nQ
);

  JK jk_1 (.J(T), .CLOCK(CLOCK), .K(T), .PRESET(PRESET), .CLEAR(CLEAR), .Q(Q), .nQ(nQ));
endmodule
