// Logisim project MUX.circ as structural Verilog: 3 circuits, main circuit Mux-2x1
// 2x1
module Mux_2x1 (
  input  Sel,
  input  A,
  input  B,
  output S
);

  wire and_1_out, and_2_out;

  and and_1 (and_1_out, A, ~Sel);  // AND_Gate
  or or_1 (S, and_1_out, and_2_out);
  and and_2 (and_2_out, B, Sel);
endmodule

module Mux_4x1 (
  input  [1:0] Sel,
  input  _0,
  input  _1,
  input  _2,
  input  _3,
  output S
);

  wire and_1_out, and_2_out, and_3_out, and_4_out;

  and and_1 (and_1_out, _0, ~Sel[1], ~Sel[0]);  // AND_Gate
  and and_2 (and_2_out, _1, ~Sel[1], Sel[0]);  // AND_Gate
  and and_3 (and_3_out, _2, Sel[1], ~Sel[0]);  // AND_Gate
  and and_4 (and_4_out, _3, Sel[1], Sel[0]);
  or or_1 (S, and_1_out, and_2_out, and_3_out, and_4_out);
endmodule

// M2x1-8b
module Mux_2x1_8bit (
  input  Seletor,
  input  [7:0] A,
  input  [7:0] B,
  output [7:0] out_4
);

  Mux_2x1 mux_2x1_1 (.A(A[0]), .B(B[0]), .Sel(Seletor), .S(out_4[0]));
  Mux_2x1 mux_2x1_2 (.A(A[1]), .B(B[1]), .Sel(Seletor), .S(out_4[1]));
  Mux_2x1 mux_2x1_3 (.A(A[2]), .B(B[2]), .Sel(Seletor), .S(out_4[2]));
  Mux_2x1 mux_2x1_4 (.A(A[3]), .B(B[3]), .Sel(Seletor), .S(out_4[3]));
  Mux_2x1 mux_2x1_5 (.A(A[4]), .B(B[4]), .Sel(Seletor), .S(out_4[4]));
  Mux_2x1 mux_2x1_6 (.A(A[5]), .B(B[5]), .Sel(Seletor), .S(out_4[5]));
  Mux_2x1 mux_2x1_7 (.A(A[6]), .B(B[6]), .Sel(Seletor), .S(out_4[6]));
  Mux_2x1 mux_2x1_8 (.A(A[7]), .B(B[7]), .Sel(Seletor), .S(out_4[7]));
endmodule
