// Logisim project ULA.circ as structural Verilog: 2 circuits, main circuit 1bit
module _1bit (
  input  BNeg,
  input  CarryIN,
  input  [1:0] Op,
  input  A,
  input  B,
  output S,
  output CarryOut
);

  wire and_1_out, mux_2x1_1_s, not_1_out, or_1_out, sum_1_p4;

  Mux_2x1 mux_2x1_1 (.A(B), .B(not_1_out), .Sel(BNeg), .S(mux_2x1_1_s));
  not not_1 (not_1_out, B);
  and and_1 (and_1_out, A, B);
  or or_1 (or_1_out, A, B);
  // SUM sum_1: pin names not known; wires that end beside it: CarryIN, A, mux_2x1_1_s, sum_1_p4, CarryOut
  Mux_4x1 mux_4x1_1 (._0(and_1_out), ._1(or_1_out), ._2(sum_1_p4), .Sel(Op), .S(S));  // open: _3
endmodule

module _2bit (
  input  BNeg,
  input  [1:0] in_2,
  input  [1:0] A,
  input  [1:0] B,
  output [1:0] out_5,
  output CarryOut
);

  wire n1bit_1_carryout;

  _1bit u_1bit_1 (
    .A(A[0]), .B(B[0]), .BNeg(BNeg), .CarryIN(BNeg), .Op(in_2), .CarryOut(n1bit_1_carryout), .S(out_5[0]));
  _1bit u_1bit_2 (
    .A(A[1]), .B(B[1]), .BNeg(BNeg), .CarryIN(n1bit_1_carryout), .Op(in_2), .CarryOut(CarryOut), .S(out_5[1]));
endmodule
