// Logisim project lib.circ as structural Verilog: 13 circuits, main circuit MUX2x1
module ULA8bits (
  input  Bneg,
  input  [3:0] OP,
  input  [7:0] A,
  input  [7:0] B,
  output [7:0] S
);

  wire [7:0] AND_out, c2_1_c2, c2_1_not, equal_1_s, mux2x1_1_s, OR_out, slt8bits_1_s, sum8bit_1_s;

  MUX2x1 mux2x1_1 (.A(B), .B(c2_1_c2), .OP(Bneg), .S(mux2x1_1_s));
  C2 c2_1 (.B(B), .NOT(c2_1_not), .C2(c2_1_c2));
  SUM8bit sum8bit_1 (.A(A), .B(mux2x1_1_s), .S(sum8bit_1_s));  // open: OVERFLOW
  assign AND_out = A & mux2x1_1_s;  // AND_Gate AND, 8 bits wide
  assign OR_out = A | mux2x1_1_s;  // OR_Gate OR, 8 bits wide
  SLT8bits slt8bits_1 (.A(A), .B(mux2x1_1_s), .S(slt8bits_1_s));
  EQUAL equal_1 (.A(A), .B(mux2x1_1_s), .S(equal_1_s));
  MUX16x1 mux16x1_1 (
    .A(sum8bit_1_s), .B(AND_out), .C(OR_out), .D(slt8bits_1_s), .E(equal_1_s), .F(c2_1_not), .G({8{1'b0}}),
    .H({8{1'b0}}), .I({8{1'b0}}), .J({8{1'b0}}), .K({8{1'b0}}), .L({8{1'b0}}), .M({8{1'b0}}), .N({8{1'b0}}),
    .O({8{1'b0}}), .P({8{1'b0}}), .OP(OP), .out_18(S));
endmodule

// MUX
module MUX2x1 (
  input  OP,
  input  [7:0] A,
  input  [7:0] B,
  output [7:0] S
);

  wire and_1_out, and_2_out, and_3_out, and_4_out, and_5_out, and_6_out, and_7_out, and_8_out, and_9_out,
       and_10_out, and_11_out, and_12_out, and_13_out, and_14_out, and_15_out, and_16_out;

  and and_1 (and_1_out, A[7], ~OP);  // AND_Gate
  and and_2 (and_2_out, B[7], OP);
  and and_3 (and_3_out, A[6], ~OP);  // AND_Gate
  and and_4 (and_4_out, B[6], OP);
  and and_5 (and_5_out, A[5], ~OP);  // AND_Gate
  and and_6 (and_6_out, B[5], OP);
  and and_7 (and_7_out, A[4], ~OP);  // AND_Gate
  and and_8 (and_8_out, B[4], OP);
  and and_9 (and_9_out, A[3], ~OP);  // AND_Gate
  and and_10 (and_10_out, B[3], OP);
  and and_11 (and_11_out, A[2], ~OP);  // AND_Gate
  and and_12 (and_12_out, B[2], OP);
  and and_13 (and_13_out, A[1], ~OP);  // AND_Gate
  and and_14 (and_14_out, B[1], OP);
  and and_15 (and_15_out, A[0], ~OP);  // AND_Gate
  and and_16 (and_16_out, B[0], OP);
  or or_1 (S[7], and_1_out, and_2_out);
  or or_2 (S[6], and_3_out, and_4_out);
  or or_3 (S[5], and_5_out, and_6_out);
  or or_4 (S[4], and_7_out, and_8_out);
  or or_5 (S[3], and_9_out, and_10_out);
  or or_6 (S[2], and_11_out, and_12_out);
  or or_7 (S[1], and_13_out, and_14_out);
  or or_8 (S[0], and_15_out, and_16_out);
endmodule

// MUX
module MUX4x1 (
  input  [1:0] in_1,
  input  [7:0] A,
  input  [7:0] B,
  input  [7:0] C,
  input  [7:0] D,
  output [7:0] out_6
);

  wire [7:0] mux2x1_1_s, mux2x1_3_s;

  MUX2x1 mux2x1_1 (.A(A), .B(B), .OP(in_1[0]), .S(mux2x1_1_s));
  MUX2x1 mux2x1_2 (.A(mux2x1_1_s), .B(mux2x1_3_s), .OP(in_1[1]), .S(out_6));
  MUX2x1 mux2x1_3 (.A(C), .B(D), .OP(in_1[0]), .S(mux2x1_3_s));
endmodule

// MUX
module MUX8x1 (
  input  [2:0] OP,
  input  [7:0] A,
  input  [7:0] B,
  input  [7:0] C,
  input  [7:0] D,
  input  [7:0] E,
  input  [7:0] F,
  input  [7:0] G,
  input  [7:0] H,
  output [7:0] S
);

  wire [7:0] mux4x1_1_out_6, mux4x1_2_out_6;

  MUX4x1 mux4x1_1 (.A(A), .B(B), .C(C), .D(D), .in_1(OP[1:0]), .out_6(mux4x1_1_out_6));
  MUX4x1 mux4x1_2 (.A(E), .B(F), .C(G), .D(H), .in_1(OP[1:0]), .out_6(mux4x1_2_out_6));
  MUX2x1 mux2x1_1 (.A(mux4x1_1_out_6), .B(mux4x1_2_out_6), .OP(OP[2]), .S(S));
endmodule

// MUX
module MUX16x1 (
  input  [3:0] OP,
  input  [7:0] A,
  input  [7:0] B,
  input  [7:0] C,
  input  [7:0] D,
  input  [7:0] E,
  input  [7:0] F,
  input  [7:0] G,
  input  [7:0] H,
  input  [7:0] I,
  input  [7:0] J,
  input  [7:0] K,
  input  [7:0] L,
  input  [7:0] M,
  input  [7:0] N,
  input  [7:0] O,
  input  [7:0] P,
  output [7:0] out_18
);

  wire [7:0] mux8x1_1_s, mux8x1_2_s;

  MUX8x1 mux8x1_1 (.A(A), .B(B), .C(C), .D(D), .E(E), .F(F), .G(G), .H(H), .OP(OP[2:0]), .S(mux8x1_1_s));
  MUX8x1 mux8x1_2 (.A(I), .B(J), .C(K), .D(L), .E(M), .F(N), .G(O), .H(P), .OP(OP[2:0]), .S(mux8x1_2_s));
  MUX2x1 mux2x1_1 (.A(mux8x1_1_s), .B(mux8x1_2_s), .OP(OP[3]), .S(out_18));
endmodule

// 1/2
module _1_2SUM (
  input  A,
  input  B,
  output S,
  output VAI_1
);

  xor xor_1 (S, A, B);
  and and_1 (VAI_1, A, B);
endmodule

// SUM
module SUM1bit (
  input  A,
  input  B,
  input  VEM1,
  output S,
  output VAI_1
);

  wire and_1_out, and_2_out, and_3_out, xor_1_out;

  xor xor_1 (xor_1_out, A, B);
  and and_1 (and_1_out, A, B);
  and and_2 (and_2_out, A, VEM1);
  and and_3 (and_3_out, B, VEM1);
  xor xor_2 (S, xor_1_out, VEM1);
  or or_1 (VAI_1, and_1_out, and_2_out, and_3_out);
endmodule

// +
module SUM8bit (
  input  [7:0] A,
  input  [7:0] B,
  output OVERFLOW,
  output [7:0] S
);

  wire n1_2sum_1_vai_1, sum1bit_2_vai_1, sum1bit_3_vai_1, sum1bit_4_vai_1, sum1bit_5_vai_1, sum1bit_6_vai_1,
       sum1bit_7_vai_1;

  SUM1bit sum1bit_1 (.A(A[7]), .B(B[7]), .VAI_1(OVERFLOW), .VEM1(sum1bit_2_vai_1), .S(S[7]));
  SUM1bit sum1bit_2 (.A(A[6]), .B(B[6]), .VAI_1(sum1bit_2_vai_1), .VEM1(sum1bit_3_vai_1), .S(S[6]));
  SUM1bit sum1bit_3 (.A(A[5]), .B(B[5]), .VAI_1(sum1bit_3_vai_1), .VEM1(sum1bit_4_vai_1), .S(S[5]));
  SUM1bit sum1bit_4 (.A(A[4]), .B(B[4]), .VAI_1(sum1bit_4_vai_1), .VEM1(sum1bit_5_vai_1), .S(S[4]));
  SUM1bit sum1bit_5 (.A(A[3]), .B(B[3]), .VAI_1(sum1bit_5_vai_1), .VEM1(sum1bit_6_vai_1), .S(S[3]));
  SUM1bit sum1bit_6 (.A(A[2]), .B(B[2]), .VAI_1(sum1bit_6_vai_1), .VEM1(sum1bit_7_vai_1), .S(S[2]));
  SUM1bit sum1bit_7 (.A(A[1]), .B(B[1]), .VAI_1(sum1bit_7_vai_1), .VEM1(n1_2sum_1_vai_1), .S(S[1]));
  _1_2SUM u_1_2sum_1 (.A(A[0]), .B(B[0]), .VAI_1(n1_2sum_1_vai_1), .S(S[0]));
endmodule

// SLT
module SLT8bits (
  input  [7:0] A,
  input  [7:0] B,
  output [7:0] S
);

  wire slt_eqin_1_s, slt_eqout_1_eq, slt_eqout_1_s;

  SLT_EqOUT slt_eqout_1 (.A(A[7:4]), .B(B[7:4]), .Eq(slt_eqout_1_eq), .S(slt_eqout_1_s));
  SLT_EqIN slt_eqin_1 (.A(A[3:0]), .B(B[3:0]), .Eq(slt_eqout_1_eq), .S(slt_eqin_1_s));
  or or_1 (S[7], slt_eqout_1_s, slt_eqin_1_s);

  assign S[6:0] = {7{S[7]}};
endmodule

// 1/2
module SLT_EqOUT (
  input  [3:0] A,
  input  [3:0] B,
  output S,
  output Eq
);

  wire and_1_out, and_2_out, and_3_out, and_4_out, and_5_out, and_6_out, and_7_out, xnor_1_out, xnor_2_out,
       xnor_3_out;

  and and_1 (and_1_out, ~A[3], B[3]);  // AND_Gate
  xnor xnor_1 (xnor_1_out, A[3], B[3]);
  and and_2 (and_2_out, ~A[2], B[2]);  // AND_Gate
  xnor xnor_2 (xnor_2_out, A[2], B[2]);
  and and_3 (and_3_out, ~A[1], B[1]);  // AND_Gate
  xnor xnor_3 (xnor_3_out, A[1], B[1]);
  and and_4 (and_4_out, ~A[0], B[0]);  // AND_Gate
  and and_5 (and_5_out, xnor_1_out, and_2_out);
  and and_6 (and_6_out, xnor_1_out, xnor_2_out, and_3_out);
  and and_7 (and_7_out, xnor_1_out, xnor_2_out, xnor_3_out, and_4_out);
  and and_8 (Eq, xnor_1_out, xnor_2_out, xnor_3_out);
  or or_1 (S, and_1_out, and_5_out, and_6_out, and_7_out);
endmodule

// SLT
module SLT_EqIN (
  input  Eq,
  input  [3:0] A,
  input  [3:0] B,
  output S
);

  wire and_1_out, and_2_out, and_3_out, and_4_out, and_5_out, and_6_out, and_7_out, xnor_1_out, xnor_2_out,
       xnor_3_out;

  and and_1 (and_1_out, ~A[3], Eq, B[3]);  // AND_Gate
  xnor xnor_1 (xnor_1_out, A[3], B[3]);
  and and_2 (and_2_out, ~A[2], B[2]);  // AND_Gate
  xnor xnor_2 (xnor_2_out, A[2], B[2]);
  and and_3 (and_3_out, ~A[1], B[1]);  // AND_Gate
  xnor xnor_3 (xnor_3_out, A[1], B[1]);
  and and_4 (and_4_out, ~A[0], B[0]);  // AND_Gate
  and and_5 (and_5_out, xnor_1_out, Eq, and_2_out);
  and and_6 (and_6_out, Eq, xnor_1_out, xnor_2_out, and_3_out);
  and and_7 (and_7_out, xnor_1_out, xnor_2_out, Eq, xnor_3_out, and_4_out);
  or or_1 (S, and_1_out, and_5_out, and_6_out, and_7_out);
endmodule

module C2 (
  input  [7:0] B,
  output [7:0] C2,
  output [7:0] NOT
);

  wire n1_2sum_1_vai_1, not_2_out, sum1bit_2_vai_1, sum1bit_3_vai_1, sum1bit_4_vai_1, sum1bit_5_vai_1,
       sum1bit_6_vai_1, sum1bit_7_vai_1;

  assign NOT = ~B;  // NOT_Gate not_1, 8 bits wide
  not not_2 (not_2_out, 1'b1);
  SUM1bit sum1bit_1 (.A(NOT[7]), .B(not_2_out), .VEM1(sum1bit_2_vai_1), .S(C2[7]));  // open: VAI_1
  SUM1bit sum1bit_2 (.A(NOT[6]), .B(not_2_out), .VAI_1(sum1bit_2_vai_1), .VEM1(sum1bit_3_vai_1), .S(C2[6]));
  SUM1bit sum1bit_3 (.A(NOT[5]), .B(not_2_out), .VAI_1(sum1bit_3_vai_1), .VEM1(sum1bit_4_vai_1), .S(C2[5]));
  SUM1bit sum1bit_4 (.A(NOT[4]), .B(not_2_out), .VAI_1(sum1bit_4_vai_1), .VEM1(sum1bit_5_vai_1), .S(C2[4]));
  SUM1bit sum1bit_5 (.A(NOT[3]), .B(not_2_out), .VAI_1(sum1bit_5_vai_1), .VEM1(sum1bit_6_vai_1), .S(C2[3]));
  SUM1bit sum1bit_6 (.A(NOT[2]), .B(not_2_out), .VAI_1(sum1bit_6_vai_1), .VEM1(sum1bit_7_vai_1), .S(C2[2]));
  SUM1bit sum1bit_7 (.A(NOT[1]), .B(not_2_out), .VAI_1(sum1bit_7_vai_1), .VEM1(n1_2sum_1_vai_1), .S(C2[1]));
  _1_2SUM u_1_2sum_1 (.A(NOT[0]), .B(1'b1), .VAI_1(n1_2sum_1_vai_1), .S(C2[0]));
endmodule

// EQ
module EQUAL (
  input  [7:0] A,
  input  [7:0] B,
  output [7:0] S
);

  wire xnor_1_out, xnor_2_out, xnor_3_out, xnor_4_out, xnor_5_out, xnor_6_out, xnor_7_out, xnor_8_out;

  xnor xnor_1 (xnor_1_out, A[0], B[0]);
  xnor xnor_2 (xnor_2_out, A[1], B[1]);
  xnor xnor_3 (xnor_3_out, A[2], B[2]);
  xnor xnor_4 (xnor_4_out, A[3], B[3]);
  xnor xnor_5 (xnor_5_out, A[4], B[4]);
  xnor xnor_6 (xnor_6_out, A[5], B[5]);
  xnor xnor_7 (xnor_7_out, A[6], B[6]);
  xnor xnor_8 (xnor_8_out, A[7], B[7]);
  and and_1 (S[7], xnor_1_out, xnor_2_out, xnor_3_out, xnor_4_out, xnor_5_out, xnor_6_out, xnor_7_out, xnor_8_out);

  assign S[6:0] = {7{S[7]}};
endmodule
