// Logisim project memorybank.circ as structural Verilog: 1 circuit, main circuit MB
module MB (
  input  [3:0] Reg_A,
  input  [3:0] Reg_B,
  input  [3:0] Escreve_Reg,
  input  habilita_escrita,
  input  [7:0] Dado,
  input  Preset,
  input  Clear,
  output [7:0] Dado_1,
  output [7:0] Dado_2
);

  wire dmux_1x16_1bit_1_p3, dmux_1x16_1bit_1_p4, dmux_1x16_1bit_1_p5, dmux_1x16_1bit_1_p6,
       dmux_1x16_1bit_1_p7, dmux_1x16_1bit_1_p8, dmux_1x16_1bit_1_p9, dmux_1x16_1bit_1_p10,
       dmux_1x16_1bit_1_p11, dmux_1x16_1bit_1_p12, dmux_1x16_1bit_1_p13, dmux_1x16_1bit_1_p14,
       dmux_1x16_1bit_1_p15, dmux_1x16_1bit_1_p16, dmux_1x16_1bit_1_p17, dmux_1x16_1bit_1_p18;
  wire [7:0] d_113_p5, d_114_p5, d_115_p5, d_116_p5, d_117_p5, d_118_p5, d_119_p5, d_120_p5, d_121_p5,
       d_122_p5, d_123_p5, d_124_p5, d_125_p5, d_126_p5, d_127_p5, d_128_p5;

  // dMUX_1x16__1bit dmux_1x16_1bit_1: pin names not known; wires that end beside it: habilita_escrita, Escreve_Reg, dmux_1x16_1bit_1_p3, dmux_1x16_1bit_1_p4, dmux_1x16_1bit_1_p5, dmux_1x16_1bit_1_p6, dmux_1x16_1bit_1_p7, dmux_1x16_1bit_1_p8, dmux_1x16_1bit_1_p9, dmux_1x16_1bit_1_p10, dmux_1x16_1bit_1_p11, dmux_1x16_1bit_1_p12, dmux_1x16_1bit_1_p13, dmux_1x16_1bit_1_p14, dmux_1x16_1bit_1_p15, dmux_1x16_1bit_1_p16, dmux_1x16_1bit_1_p17, dmux_1x16_1bit_1_p18
  // D d_1: pin names not known; wires that end beside it: dmux_1x16_1bit_1_p3, Preset, Clear, d_113_p5[7]
  // D d_2: pin names not known; wires that end beside it: dmux_1x16_1bit_1_p4, Preset, Clear, d_114_p5[7]
  // D d_3: pin names not known; wires that end beside it: dmux_1x16_1bit_1_p5, Preset, Clear, d_115_p5[7]
  // D d_4: pin names not known; wires that end beside it: dmux_1x16_1bit_1_p6, Preset, Clear, d_116_p5[7]
  // D d_5: pin names not known; wires that end beside it: dmux_1x16_1bit_1_p7, Preset, Clear, d_117_p5[7]
  // D d_6: pin names not known; wires that end beside it: dmux_1x16_1bit_1_p8, Preset, Clear, d_118_p5[7]
  // D d_7: pin names not known; wires that end beside it: dmux_1x16_1bit_1_p9, Preset, Clear, d_119_p5[7]
  // D d_8: pin names not known; wires that end beside it: dmux_1x16_1bit_1_p10, Preset, Clear, d_120_p5[7]
  // D d_9: pin names not known; wires that end beside it: dmux_1x16_1bit_1_p11, Preset, Clear, d_121_p5[7]
  // D d_10: pin names not known; wires that end beside it: dmux_1x16_1bit_1_p12, Preset, Clear, d_122_p5[7]
  // D d_11: pin names not known; wires that end beside it: dmux_1x16_1bit_1_p13, Preset, Clear, d_123_p5[7]
  // D d_12: pin names not known; wires that end beside it: dmux_1x16_1bit_1_p14, Preset, Clear, d_124_p5[7]
  // D d_13: pin names not known; wires that end beside it: dmux_1x16_1bit_1_p15, Preset, Clear, d_125_p5[7]
  // D d_14: pin names not known; wires that end beside it: dmux_1x16_1bit_1_p16, Preset, Clear, d_126_p5[7]
  // D d_15: pin names not known; wires that end beside it: dmux_1x16_1bit_1_p17, Preset, Clear, d_127_p5[7]
  // D d_16: pin names not known; wires that end beside it: dmux_1x16_1bit_1_p18, Preset, Clear, d_128_p5[7]
  // D d_17: pin names not known; wires that end beside it: d_113_p5[7], dmux_1x16_1bit_1_p3, Preset, Clear, d_113_p5[6]
  // D d_18: pin names not known; wires that end beside it: d_114_p5[7], dmux_1x16_1bit_1_p4, Preset, Clear, d_114_p5[6]
  // D d_19: pin names not known; wires that end beside it: d_115_p5[7], dmux_1x16_1bit_1_p5, Preset, Clear, d_115_p5[6]
  // D d_20: pin names not known; wires that end beside it: d_116_p5[7], dmux_1x16_1bit_1_p6, Preset, Clear, d_116_p5[6]
  // D d_21: pin names not known; wires that end beside it: d_117_p5[7], dmux_1x16_1bit_1_p7, Preset, Clear, d_117_p5[6]
  // D d_22: pin names not known; wires that end beside it: d_118_p5[7], dmux_1x16_1bit_1_p8, Preset, Clear, d_118_p5[6]
  // D d_23: pin names not known; wires that end beside it: d_119_p5[7], dmux_1x16_1bit_1_p9, Preset, Clear, d_119_p5[6]
  // D d_24: pin names not known; wires that end beside it: d_120_p5[7], dmux_1x16_1bit_1_p10, Preset, Clear, d_120_p5[6]
  // D d_25: pin names not known; wires that end beside it: d_121_p5[7], dmux_1x16_1bit_1_p11, Preset, Clear, d_121_p5[6]
  // D d_26: pin names not known; wires that end beside it: d_122_p5[7], dmux_1x16_1bit_1_p12, Preset, Clear, d_122_p5[6]
  // D d_27: pin names not known; wires that end beside it: d_123_p5[7], dmux_1x16_1bit_1_p13, Preset, Clear, d_123_p5[6]
  // D d_28: pin names not known; wires that end beside it: d_124_p5[7], dmux_1x16_1bit_1_p14, Preset, Clear, d_124_p5[6]
  // D d_29: pin names not known; wires that end beside it: d_125_p5[7], dmux_1x16_1bit_1_p15, Preset, Clear, d_125_p5[6]
  // D d_30: pin names not known; wires that end beside it: d_126_p5[7], dmux_1x16_1bit_1_p16, Preset, Clear, d_126_p5[6]
  // D d_31: pin names not known; wires that end beside it: d_127_p5[7], dmux_1x16_1bit_1_p17, Preset, Clear, d_127_p5[6]
  // D d_32: pin names not known; wires that end beside it: d_128_p5[7], dmux_1x16_1bit_1_p18, Preset, Clear, d_128_p5[6]
  // D d_33: pin names not known; wires that end beside it: d_113_p5[6], dmux_1x16_1bit_1_p3, Preset, Clear, d_113_p5[5]
  // D d_34: pin names not known; wires that end beside it: d_114_p5[6], dmux_1x16_1bit_1_p4, Preset, Clear, d_114_p5[5]
  // D d_35: pin names not known; wires that end beside it: d_115_p5[6], dmux_1x16_1bit_1_p5, Preset, Clear, d_115_p5[5]
  // D d_36: pin names not known; wires that end beside it: d_116_p5[6], dmux_1x16_1bit_1_p6, Preset, Clear, d_116_p5[5]
  // D d_37: pin names not known; wires that end beside it: d_117_p5[6], dmux_1x16_1bit_1_p7, Preset, Clear, d_117_p5[5]
  // D d_38: pin names not known; wires that end beside it: d_118_p5[6], dmux_1x16_1bit_1_p8, Preset, Clear, d_118_p5[5]
  // D d_39: pin names not known; wires that end beside it: d_119_p5[6], dmux_1x16_1bit_1_p9, Preset, Clear, d_119_p5[5]
  // D d_40: pin names not known; wires that end beside it: d_120_p5[6], dmux_1x16_1bit_1_p10, Preset, Clear, d_120_p5[5]
  // D d_41: pin names not known; wires that end beside it: d_121_p5[6], dmux_1x16_1bit_1_p11, Preset, Clear, d_121_p5[5]
  // D d_42: pin names not known; wires that end beside it: d_122_p5[6], dmux_1x16_1bit_1_p12, Preset, Clear, d_122_p5[5]
  // D d_43: pin names not known; wires that end beside it: d_123_p5[6], dmux_1x16_1bit_1_p13, Preset, Clear, d_123_p5[5]
  // D d_44: pin names not known; wires that end beside it: d_124_p5[6], dmux_1x16_1bit_1_p14, Preset, Clear, d_124_p5[5]
  // D d_45: pin names not known; wires that end beside it: d_125_p5[6], dmux_1x16_1bit_1_p15, Preset, Clear, d_125_p5[5]
  // D d_46: pin names not known; wires that end beside it: d_126_p5[6], dmux_1x16_1bit_1_p16, Preset, Clear, d_126_p5[5]
  // D d_47: pin names not known; wires that end beside it: d_127_p5[6], dmux_1x16_1bit_1_p17, Preset, Clear, d_127_p5[5]
  // D d_48: pin names not known; wires that end beside it: d_128_p5[6], dmux_1x16_1bit_1_p18, Preset, Clear, d_128_p5[5]
  // D d_49: pin names not known; wires that end beside it: d_113_p5[5], dmux_1x16_1bit_1_p3, Preset, Clear, d_113_p5[4], dmux_1x16_1bit_1_p3
  // D d_50: pin names not known; wires that end beside it: d_113_p5[4], dmux_1x16_1bit_1_p3, Preset, Clear, d_113_p5[3]
  // D d_51: pin names not known; wires that end beside it: d_114_p5[5], dmux_1x16_1bit_1_p4, Preset, Clear, d_114_p5[4], dmux_1x16_1bit_1_p4
  // D d_52: pin names not known; wires that end beside it: d_114_p5[4], dmux_1x16_1bit_1_p4, Preset, Clear, d_114_p5[3]
  // D d_53: pin names not known; wires that end beside it: d_115_p5[5], dmux_1x16_1bit_1_p5, Preset, Clear, d_115_p5[4], dmux_1x16_1bit_1_p5
  // D d_54: pin names not known; wires that end beside it: d_115_p5[4], dmux_1x16_1bit_1_p5, Preset, Clear, d_115_p5[3]
  // D d_55: pin names not known; wires that end beside it: d_116_p5[4], dmux_1x16_1bit_1_p6, Preset, Clear, d_116_p5[3]
  // D d_56: pin names not known; wires that end beside it: d_116_p5[5], dmux_1x16_1bit_1_p6, Preset, Clear, d_116_p5[4], dmux_1x16_1bit_1_p6
  // D d_57: pin names not known; wires that end beside it: d_117_p5[5], dmux_1x16_1bit_1_p7, Preset, Clear, d_117_p5[4], dmux_1x16_1bit_1_p7
  // D d_58: pin names not known; wires that end beside it: d_117_p5[4], dmux_1x16_1bit_1_p7, Preset, Clear, d_117_p5[3]
  // D d_59: pin names not known; wires that end beside it: d_118_p5[5], dmux_1x16_1bit_1_p8, Preset, Clear, d_118_p5[4], dmux_1x16_1bit_1_p8
  // D d_60: pin names not known; wires that end beside it: d_118_p5[4], dmux_1x16_1bit_1_p8, Preset, Clear, d_118_p5[3]
  // D d_61: pin names not known; wires that end beside it: d_119_p5[4], dmux_1x16_1bit_1_p9, Preset, Clear, d_119_p5[3]
  // D d_62: pin names not known; wires that end beside it: d_119_p5[5], dmux_1x16_1bit_1_p9, Preset, Clear, d_119_p5[4], dmux_1x16_1bit_1_p9
  // D d_63: pin names not known; wires that end beside it: d_120_p5[4], dmux_1x16_1bit_1_p10, Preset, Clear, d_120_p5[3]
  // D d_64: pin names not known; wires that end beside it: d_120_p5[5], dmux_1x16_1bit_1_p10, Preset, Clear, d_120_p5[4], dmux_1x16_1bit_1_p10
  // D d_65: pin names not known; wires that end beside it: d_121_p5[5], dmux_1x16_1bit_1_p11, Preset, Clear, d_121_p5[4], dmux_1x16_1bit_1_p11
  // D d_66: pin names not known; wires that end beside it: d_121_p5[4], dmux_1x16_1bit_1_p11, Preset, Clear, d_121_p5[3]
  // D d_67: pin names not known; wires that end beside it: d_122_p5[4], dmux_1x16_1bit_1_p12, Preset, Clear, d_122_p5[3]
  // D d_68: pin names not known; wires that end beside it: d_122_p5[5], dmux_1x16_1bit_1_p12, Preset, Clear, d_122_p5[4], dmux_1x16_1bit_1_p12
  // D d_69: pin names not known; wires that end beside it: d_123_p5[5], dmux_1x16_1bit_1_p13, Preset, Clear, d_123_p5[4], dmux_1x16_1bit_1_p13
  // D d_70: pin names not known; wires that end beside it: d_123_p5[4], dmux_1x16_1bit_1_p13, Preset, Clear, d_123_p5[3]
  // D d_71: pin names not known; wires that end beside it: d_124_p5[4], dmux_1x16_1bit_1_p14, Preset, Clear, d_124_p5[3]
  // D d_72: pin names not known; wires that end beside it: d_124_p5[5], dmux_1x16_1bit_1_p14, Preset, Clear, d_124_p5[4], dmux_1x16_1bit_1_p14
  // D d_73: pin names not known; wires that end beside it: d_125_p5[5], dmux_1x16_1bit_1_p15, Preset, Clear, d_125_p5[4], dmux_1x16_1bit_1_p15
  // D d_74: pin names not known; wires that end beside it: d_125_p5[4], dmux_1x16_1bit_1_p15, Preset, Clear, d_125_p5[3]
  // D d_75: pin names not known; wires that end beside it: d_126_p5[5], dmux_1x16_1bit_1_p16, Preset, Clear, d_126_p5[4], dmux_1x16_1bit_1_p16
  // D d_76: pin names not known; wires that end beside it: d_126_p5[4], dmux_1x16_1bit_1_p16, Preset, Clear, d_126_p5[3]
  // D d_77: pin names not known; wires that end beside it: d_127_p5[5], dmux_1x16_1bit_1_p17, Preset, Clear, d_127_p5[4], dmux_1x16_1bit_1_p17
  // D d_78: pin names not known; wires that end beside it: d_127_p5[4], dmux_1x16_1bit_1_p17, Preset, Clear, d_127_p5[3]
  // D d_79: pin names not known; wires that end beside it: d_128_p5[4], dmux_1x16_1bit_1_p18, Preset, Clear, d_128_p5[3]
  // D d_80: pin names not known; wires that end beside it: d_128_p5[5], dmux_1x16_1bit_1_p18, Preset, Clear, d_128_p5[4], dmux_1x16_1bit_1_p18
  // D d_81: pin names not known; wires that end beside it: d_113_p5[3], dmux_1x16_1bit_1_p3, Preset, Clear, d_113_p5[2]
  // D d_82: pin names not known; wires that end beside it: d_114_p5[3], dmux_1x16_1bit_1_p4, Preset, Clear, d_114_p5[2]
  // D d_83: pin names not known; wires that end beside it: d_115_p5[3], dmux_1x16_1bit_1_p5, Preset, Clear, d_115_p5[2]
  // D d_84: pin names not known; wires that end beside it: d_116_p5[3], dmux_1x16_1bit_1_p6, Preset, Clear, d_116_p5[2]
  // D d_85: pin names not known; wires that end beside it: d_117_p5[3], dmux_1x16_1bit_1_p7, Preset, Clear, d_117_p5[2]
  // D d_86: pin names not known; wires that end beside it: d_118_p5[3], dmux_1x16_1bit_1_p8, Preset, Clear, d_118_p5[2]
  // D d_87: pin names not known; wires that end beside it: d_119_p5[3], dmux_1x16_1bit_1_p9, Preset, Clear, d_119_p5[2]
  // D d_88: pin names not known; wires that end beside it: d_120_p5[3], dmux_1x16_1bit_1_p10, Preset, Clear, d_120_p5[2]
  // D d_89: pin names not known; wires that end beside it: d_121_p5[3], dmux_1x16_1bit_1_p11, Preset, Clear, d_121_p5[2]
  // D d_90: pin names not known; wires that end beside it: d_122_p5[3], dmux_1x16_1bit_1_p12, Preset, Clear, d_122_p5[2]
  // D d_91: pin names not known; wires that end beside it: d_123_p5[3], dmux_1x16_1bit_1_p13, Preset, Clear, d_123_p5[2]
  // D d_92: pin names not known; wires that end beside it: d_124_p5[3], dmux_1x16_1bit_1_p14, Preset, Clear, d_124_p5[2]
  // D d_93: pin names not known; wires that end beside it: d_125_p5[3], dmux_1x16_1bit_1_p15, Preset, Clear, d_125_p5[2]
  // D d_94: pin names not known; wires that end beside it: d_126_p5[3], dmux_1x16_1bit_1_p16, Preset, Clear, d_126_p5[2]
  // D d_95: pin names not known; wires that end beside it: d_127_p5[3], dmux_1x16_1bit_1_p17, Preset, Clear, d_127_p5[2]
  // D d_96: pin names not known; wires that end beside it: d_128_p5[3], dmux_1x16_1bit_1_p18, Preset, Clear, d_128_p5[2]
  // D d_97: pin names not known; wires that end beside it: d_113_p5[2], dmux_1x16_1bit_1_p3, Preset, Clear, d_113_p5[1]
  // D d_98: pin names not known; wires that end beside it: d_114_p5[2], dmux_1x16_1bit_1_p4, Preset, Clear, d_114_p5[1]
  // D d_99: pin names not known; wires that end beside it: d_115_p5[2], dmux_1x16_1bit_1_p5, Preset, Clear, d_115_p5[1]
  // D d_100: pin names not known; wires that end beside it: d_116_p5[2], dmux_1x16_1bit_1_p6, Preset, Clear, d_116_p5[1]
  // D d_101: pin names not known; wires that end beside it: d_117_p5[2], dmux_1x16_1bit_1_p7, Preset, Clear, d_117_p5[1]
  // D d_102: pin names not known; wires that end beside it: d_118_p5[2], dmux_1x16_1bit_1_p8, Preset, Clear, d_118_p5[1]
  // D d_103: pin names not known; wires that end beside it: d_119_p5[2], dmux_1x16_1bit_1_p9, Preset, Clear, d_119_p5[1]
  // D d_104: pin names not known; wires that end beside it: d_120_p5[2], dmux_1x16_1bit_1_p10, Preset, Clear, d_120_p5[1]
  // D d_105: pin names not known; wires that end beside it: d_121_p5[2], dmux_1x16_1bit_1_p11, Preset, Clear, d_121_p5[1]
  // D d_106: pin names not known; wires that end beside it: d_122_p5[2], dmux_1x16_1bit_1_p12, Preset, Clear, d_122_p5[1]
  // D d_107: pin names not known; wires that end beside it: d_123_p5[2], dmux_1x16_1bit_1_p13, Preset, Clear, d_123_p5[1]
  // D d_108: pin names not known; wires that end beside it: d_124_p5[2], dmux_1x16_1bit_1_p14, Preset, Clear, d_124_p5[1]
  // D d_109: pin names not known; wires that end beside it: d_125_p5[2], dmux_1x16_1bit_1_p15, Preset, Clear, d_125_p5[1]
  // D d_110: pin names not known; wires that end beside it: d_126_p5[2], dmux_1x16_1bit_1_p16, Preset, Clear, d_126_p5[1]
  // D d_111: pin names not known; wires that end beside it: d_127_p5[2], dmux_1x16_1bit_1_p17, Preset, Clear, d_127_p5[1]
  // D d_112: pin names not known; wires that end beside it: d_128_p5[2], dmux_1x16_1bit_1_p18, Preset, Clear, d_128_p5[1]
  // D d_113: pin names not known; wires that end beside it: d_113_p5[1], dmux_1x16_1bit_1_p3, Preset, Clear, d_113_p5[0]
  // D d_114: pin names not known; wires that end beside it: d_114_p5[1], dmux_1x16_1bit_1_p4, Preset, Clear, d_114_p5[0]
  // D d_115: pin names not known; wires that end beside it: d_115_p5[1], dmux_1x16_1bit_1_p5, Preset, Clear, d_115_p5[0]
  // D d_116: pin names not known; wires that end beside it: d_116_p5[1], dmux_1x16_1bit_1_p6, Preset, Clear, d_116_p5[0]
  // D d_117: pin names not known; wires that end beside it: d_117_p5[1], dmux_1x16_1bit_1_p7, Preset, Clear, d_117_p5[0]
  // D d_118: pin names not known; wires that end beside it: d_118_p5[1], dmux_1x16_1bit_1_p8, Preset, Clear, d_118_p5[0]
  // D d_119: pin names not known; wires that end beside it: d_119_p5[1], dmux_1x16_1bit_1_p9, Preset, Clear, d_119_p5[0]
  // D d_120: pin names not known; wires that end beside it: d_120_p5[1], dmux_1x16_1bit_1_p10, Preset, Clear, d_120_p5[0]
  // D d_121: pin names not known; wires that end beside it: d_121_p5[1], dmux_1x16_1bit_1_p11, Preset, Clear, d_121_p5[0]
  // D d_122: pin names not known; wires that end beside it: d_122_p5[1], dmux_1x16_1bit_1_p12, Preset, Clear, d_122_p5[0]
  // D d_123: pin names not known; wires that end beside it: d_123_p5[1], dmux_1x16_1bit_1_p13, Preset, Clear, d_123_p5[0]
  // D d_124: pin names not known; wires that end beside it: d_124_p5[1], dmux_1x16_1bit_1_p14, Preset, Clear, d_124_p5[0]
  // D d_125: pin names not known; wires that end beside it: d_125_p5[1], dmux_1x16_1bit_1_p15, Preset, Clear, d_125_p5[0]
  // D d_126: pin names not known; wires that end beside it: d_126_p5[1], dmux_1x16_1bit_1_p16, Preset, Clear, d_126_p5[0]
  // D d_127: pin names not known; wires that end beside it: d_127_p5[1], dmux_1x16_1bit_1_p17, Preset, Clear, d_127_p5[0]
  // D d_128: pin names not known; wires that end beside it: d_128_p5[1], dmux_1x16_1bit_1_p18, Preset, Clear, d_128_p5[0]
  // MUX16x1 mux16x1_1: pin names not known; wires that end beside it: d_113_p5, d_114_p5, d_115_p5, d_116_p5, d_117_p5, d_118_p5, d_119_p5, d_120_p5, d_121_p5, d_122_p5, d_123_p5, d_124_p5, d_125_p5, d_126_p5, d_127_p5, d_128_p5, Dado_1
  // MUX16x1 mux16x1_2: pin names not known; wires that end beside it: d_113_p5, d_114_p5, d_115_p5, d_116_p5, d_117_p5, d_118_p5, d_119_p5, d_120_p5, d_121_p5, d_122_p5, d_123_p5, d_124_p5, d_125_p5, d_126_p5, d_127_p5, d_128_p5, Dado_2
endmodule
