// Logisim project slt_8bits.circ as structural Verilog: 3 circuits, main circuit 1/2SLT
// 1/2
module _1_2SLT (
  input  A,
  input  B,
  output Ts,
  output Equal
);

  wire and_2_out, and_3_out, not_1_out, not_2_out, not_3_out;

  not not_1 (not_1_out, A);
  and and_1 (Ts, not_1_out, B);
  not not_2 (not_2_out, A);
  and and_2 (and_2_out, not_2_out, not_3_out);
  not not_3 (not_3_out, B);
  and and_3 (and_3_out, A, B);
  or or_1 (Equal, and_2_out, and_3_out);
endmodule

// SLT
module _1bitSLT (
  input  Equal,
  input  Te,
  input  A,
  input  B,
  output Ts,
  output Eout
);

  wire and_1_out, and_2_out, and_3_out, and_4_out, and_5_out, and_6_out, not_1_out, not_2_out, not_3_out,
       not_4_out, not_5_out, not_6_out;

  not not_1 (not_1_out, A);
  not not_2 (not_2_out, A);
  not not_3 (not_3_out, Te);
  not not_4 (not_4_out, B);
  not not_5 (not_5_out, A);
  not not_6 (not_6_out, B);
  and and_1 (and_1_out, not_1_out, B);
  and and_2 (and_2_out, Te, not_2_out);
  and and_3 (and_3_out, Equal, not_3_out, A, not_4_out);
  and and_4 (and_4_out, Equal, Te, B);
  and and_5 (and_5_out, not_5_out, not_6_out);
  and and_6 (and_6_out, A, B);
  or or_1 (Ts, and_1_out, and_2_out, and_3_out, and_4_out);
  or or_2 (Eout, and_5_out, and_6_out);
endmodule

module _8bitSLT (
  input  [7:0] A,
  input  [7:0] B,
  output a___B
);

  wire n1_2slt_1_equal, n1_2slt_1_ts, n1bitslt_2_eout, n1bitslt_2_ts, n1bitslt_3_eout, n1bitslt_3_ts,
       n1bitslt_4_eout, n1bitslt_4_ts, n1bitslt_5_eout, n1bitslt_5_ts, n1bitslt_6_eout, n1bitslt_6_ts,
       n1bitslt_7_eout, n1bitslt_7_ts;

  _1bitSLT u_1bitslt_1 (.A(A[7]), .B(B[7]), .Ts(a___B), .Te(n1bitslt_2_ts), .Equal(n1bitslt_2_eout));  // open: Eout
  _1bitSLT u_1bitslt_2 (
    .A(A[6]), .B(B[6]), .Ts(n1bitslt_2_ts), .Eout(n1bitslt_2_eout), .Te(n1bitslt_3_ts),
    .Equal(n1bitslt_3_eout));
  _1bitSLT u_1bitslt_3 (
    .A(A[5]), .B(B[5]), .Ts(n1bitslt_3_ts), .Eout(n1bitslt_3_eout), .Te(n1bitslt_4_ts),
    .Equal(n1bitslt_4_eout));
  _1bitSLT u_1bitslt_4 (
    .A(A[4]), .B(B[4]), .Ts(n1bitslt_4_ts), .Eout(n1bitslt_4_eout), .Te(n1bitslt_5_ts),
    .Equal(n1bitslt_5_eout));
  _1bitSLT u_1bitslt_5 (
    .A(A[3]), .B(B[3]), .Ts(n1bitslt_5_ts), .Eout(n1bitslt_5_eout), .Te(n1bitslt_6_ts),
    .Equal(n1bitslt_6_eout));
  _1bitSLT u_1bitslt_6 (
    .A(A[2]), .B(B[2]), .Ts(n1bitslt_6_ts), .Eout(n1bitslt_6_eout), .Te(n1bitslt_7_ts),
    .Equal(n1bitslt_7_eout));
  _1bitSLT u_1bitslt_7 (
    .A(A[1]), .B(B[1]), .Ts(n1bitslt_7_ts), .Eout(n1bitslt_7_eout), .Te(n1_2slt_1_ts), .Equal(n1_2slt_1_equal));
  _1_2SLT u_1_2slt_1 (.A(A[0]), .B(B[0]), .Ts(n1_2slt_1_ts), .Equal(n1_2slt_1_equal));
endmodule
