// Logisim project ula_8bits.circ as structural Verilog: 1 circuit, main circuit ULA
module ULA (
  input  Bneg,
  input  [3:0] OP,
  input  [7:0] A,
  input  [7:0] B,
  output [7:0] S
);

  wire c2_1_p2, equal_1_p3, mux2x1_1_p2;
  wire [7:0] AND_out, mux2x1_1_p4, OR_out, slt8bits_1_s, sum8bit_1_s;

  // MUX2x1 mux2x1_1: pin names not known; wires that end beside it: B, mux2x1_1_p2, Bneg, mux2x1_1_p4
  // C2 c2_1: pin names not known; wires that end beside it: B, c2_1_p2, mux2x1_1_p2
  SUM8bit sum8bit_1 (.A(A), .B(mux2x1_1_p4), .S(sum8bit_1_s));  // open: OVERFLOW
  assign AND_out = A & mux2x1_1_p4;  // AND_Gate AND, 8 bits wide
  assign OR_out = A | mux2x1_1_p4;  // OR_Gate OR, 8 bits wide
  SLT8bits slt8bits_1 (.A(A), .B(mux2x1_1_p4), .S(slt8bits_1_s));
  // EQUAL equal_1: pin names not known; wires that end beside it: A, mux2x1_1_p4, equal_1_p3
  // MUX16x1 mux16x1_1: pin names not known; wires that end beside it: sum8bit_1_s, AND_out, OR_out, slt8bits_1_s, equal_1_p3, c2_1_p2, {8{1'b0}}, {8{1'b0}}, {8{1'b0}}, {8{1'b0}}, {8{1'b0}}, {8{1'b0}}, {8{1'b0}}, {8{1'b0}}, {8{1'b0}}, {8{1'b0}}, OP, S
endmodule
