# Fritzing sketch 4bits-7Seg (saved by Fritzing 0.9.6b)
breadboards: 4

parts:
  Componente3 = DB25M
  7_Segment1 = 7 Segment Display
  7_Segment2 = 7 Segment Display
  U1 = 74HC04 NOT
  U3 = 4077 4 x 2 Input XNOR Gate, single part [part_number="4077 XNOR" package="DIP (Dual Inline) [THT]"]
  U5 = 4071 4 x 2 Input OR Gate, single part [part_number="4071 OR" package="DIP (Dual Inline) [THT]"]
  U6 = 4071 4 x 2 Input OR Gate, single part [part_number="4071 OR" package="DIP (Dual Inline) [THT]"]
  U7 = 74HC32
  U8 = 74HC32
  U9 = 4071 4 x 2 Input OR Gate, single part [part_number="4071 OR" package="DIP (Dual Inline) [THT]"]
  U10 = 74HC32

nets:
  N1: Componente3.pin9, 7_Segment1.common_cathode#12, 7_Segment1.Segment_B
  N2: Componente3.pin10, U1.1A, U3.B3, U3.B4, U5.B2, U7.4A, U8.4A, U9.A1, U10.4B
  N3: Componente3.pin11, U1.2A, U3.B1, U3.A3, U5.A4, U7.2B, U10.1A
  N4: Componente3.pin12, U1.3A, U3.A1, U3.A4, U5.A2, U10.4A
  VCC: Componente3.pin14, U1.VCC, U3.VDD, U5.VDD, U6.VDD, U7.VCC, U8.VCC, U9.VDD, U10.VCC
  GND: Componente3.pin25, 7_Segment1.common_cathode#3, 7_Segment1.common_cathode#5, 7_Segment1.common_cathode#11, 7_Segment1.common_cathode#16, 7_Segment2.common_cathode#3, 7_Segment2.common_cathode#16, U1.GND, U3.GND, U5.GND, U6.GND, U7.GND, U8.GND, U9.GND, U10.GND
  N5: 7_Segment2.Segment_A, U5.Q4
  N6: 7_Segment2.Segment_F, U6.Q3
  N7: 7_Segment2.Segment_E, U6.Q2
  N8: 7_Segment2.Segment_D, U9.Q3
  N9: 7_Segment2.common_cathode#12, U6.Q1
  N10: 7_Segment2.Segment_G, U6.Q4
  N11: 7_Segment2.Segment_B, U5.Q1
  N12: U1.1Y, U5.B1, U7.1A
  N13: U1.2Y, U5.B3, U6.B1, U7.3B, U10.2A, U10.3A
  N14: U1.3Y, U5.A3, U7.1B, U7.2A, U7.3A, U8.4B, U9.B1, U10.1B
  N15: U1.4Y, U6.B4
  N16: U1.4A, U3.Q3
  N17: U3.Q1, U5.A1
  N18: U3.Q4, U5.B4
  N19: U5.Q2, U6.A1
  N20: U5.Q3, U7.4B
  N21: U6.A2, U7.2Y
  N22: U6.B2, U7.1Y
  N23: U6.A3, U7.4Y
  N24: U6.B3, U7.3Y
  N25: U6.A4, U8.4Y
  N26: U9.Q1, U10.2B
  N27: U9.Q2, U9.A3
  N28: U9.A2, U10.2Y
  N29: U9.B2, U10.1Y
  N30: U9.B3, U10.3Y
  N31: U10.3B, U10.4Y

notes:
  =
  C
  -
  +
  msb
  lsb
  enable
  GND
  5Vcc

custom parts:
  74HC04 NOT: SNx4HC04 Hex Inverters SN54HC04, SN74HC04
  74HC32: QUADRUPLE 2-INPUT OR GATES
