# Fritzing sketch Keyboard_Octal (saved by Fritzing 0.9.6b)
breadboards: 1

parts:
  U1 = 74HC04 NOT
  U2 = 74HC04 NOT
  X2 = USB Connectors [package=usb-b-pth]
  4 = Round Pushbutton
  5 = Round Pushbutton
  6 = Round Pushbutton
  - = Round Pushbutton
  7 = Round Pushbutton
  3 = Round Pushbutton
  + = Round Pushbutton
  2 = Round Pushbutton
  1 = Round Pushbutton
  = = Round Pushbutton
  Clear = Round Pushbutton
  0 = Round Pushbutton
  Componente2 = DB25F

nets:
  N1: U1.1A, +.leg1
  N2: U1.1Y, Componente2.pin8
  N3: U1.2A, 3.leg1
  N4: U1.2Y, Componente2.pin9
  N5: U1.3A, 2.leg1
  N6: U1.3Y, Componente2.pin10
  GND: U1.GND, U2.GND, X2.GND, Componente2.pin25
  N7: U1.4Y, Componente2.pin4
  N8: U1.4A, -.leg1
  N9: U1.5A#9, Componente2.pin5
  N10: U1.5A#10, 5.leg1
  N11: U1.6Y, Componente2.pin6
  N12: U1.6A, 4.leg1
  VCC: U1.VCC, U2.VCC, X2.VBUS, 4.leg0, 5.leg0, 6.leg0, -.leg0, 7.leg0, 3.leg0, +.leg0, 2.leg0, 1.leg0, =.leg0, Clear.leg0, 0.leg0, Componente2.pin14
  N13: U2.1A, =.leg1
  N14: U2.1Y, Componente2.pin13
  N15: U2.2A, 1.leg1
  N16: U2.2Y, Componente2.pin12
  N17: U2.3A, 0.leg1
  N18: U2.3Y, Componente2.pin11
  N19: U2.4Y, Componente2.pin3
  N20: U2.4A, Clear.leg1
  N21: U2.5A#9, Componente2.pin2
  N22: U2.5A#10, 7.leg1
  N23: U2.6Y, Componente2.pin1
  N24: U2.6A, 6.leg1

notes:
  =
  +
  -
  C
  7
  6
  5
  4
  3
  2
  1
  0
  GND
  5Vcc

custom parts:
  74HC04 NOT: SNx4HC04 Hex Inverters SN54HC04, SN74HC04
  Round Pushbutton: A generic pushbutton.
