# Fritzing sketch Octal-BIN (saved by Fritzing 0.9.6b)
breadboards: 3

parts:
  Componente3 = DB25M
  U1 = 74HC32
  U2 = 74HC32
  U3 = 74HC32
  Componente4 = DB25F

nets:
  N1: Componente3.pin1, U1.4A, U2.4B
  N2: Componente3.pin2, U1.4B, U2.4A, U3.4B
  N3: Componente3.pin3, Componente4.pin3
  N4: Componente3.pin4, Componente4.pin4
  N5: Componente3.pin5, U1.1A, U3.4A
  N6: Componente3.pin6, U1.1B
  N7: Componente3.pin8, Componente4.pin8
  N8: Componente3.pin9, U2.1A, U3.1A
  N9: Componente3.pin10, U2.1B
  N10: Componente3.pin11, U1.2A
  N11: Componente3.pin12, U3.1B
  N12: Componente3.pin13, Componente4.pin13
  VCC: Componente3.pin14, U1.VCC, U2.VCC, U3.VCC, Componente4.pin14
  GND: Componente3.pin25, U1.GND, U2.GND, U3.GND, Componente4.pin25
  N13: U1.1Y, U1.3A
  N14: U1.2B, U1.3Y, Componente4.pin10
  N15: U1.2Y, U2.2A
  N16: U1.3B, U1.4Y
  N17: U2.1Y, U2.3A
  N18: U2.2B, U3.2Y
  N19: U2.2Y, Componente4.pin7
  N20: U2.3Y, U3.2A, Componente4.pin11
  N21: U2.3B, U2.4Y
  N22: U3.1Y, U3.3A
  N23: U3.2B, U3.3Y, Componente4.pin12
  N24: U3.3B, U3.4Y

notes:
  GND
  =
  0
  5Vcc
  6
  7
  C
  -
  5
  4
  +
  3
  2
  1
  msb
  lsb
  enable

custom parts:
  74HC32: QUADRUPLE 2-INPUT OR GATES
