# Fritzing sketch Rosie (saved by Fritzing 0.9.6b)
breadboards: 2

parts:
  S1 = H-Bridge with L298N
  Motor_DC_Esquerdo1 = Motor DC 6V Esquerdo
  MOTOR_DC_6V_direito1 = MOTOR_DC6V
  Componente2 = PowerBank 5v 5000mAh
  e-radionica_com1 = LM393 IR Sensor [part_number=100028]
  e-radionica_com2 = LM393 IR Sensor [part_number=100028]
  e-radionica_com3 = LM393 IR Sensor [part_number=100028]
  e-radionica_com4 = LM393 LDR breakout [part_number=100027]
  U1 = 74HC00 NAND  # not connected
  U3 = 74HC08 AND  # not connected
  U4 = 74HC32 OR  # not connected
  U5 = 74HC04 NOT  # not connected
  U6 = 74LS02P NOR  # not connected
  U7 = 74HC86 XOR  # not connected
  BAT1 = BC9VPC [package=bc9vpc]

nets:
  N1: S1.12V, BAT1.V+
  GND: S1.GND, Componente2.negative, e-radionica_com1.GND, e-radionica_com2.GND, e-radionica_com3.GND, e-radionica_com4.GND, BAT1.V-
  N2: S1.OUT3-Motor2, Motor_DC_Esquerdo1.GND
  N3: S1.OUT4-Motor2, Motor_DC_Esquerdo1.VCC
  N4: S1.OUT1-Motor1, MOTOR_DC_6V_direito1.GND
  N5: S1.OUT2-Motor1, MOTOR_DC_6V_direito1.VCC
  VCC: Componente2.positive, e-radionica_com1.VCC, e-radionica_com2.VCC, e-radionica_com3.VCC, e-radionica_com4.VCC

custom parts:
  H-Bridge with L298N: h-bridge
  Motor DC 6V Esquerdo: Motor dc esquerdo
  MOTOR_DC6V: Motor dc 6V direito
  74HC00 NAND: (74HC00; 74HCT00 ) Quad 2-input NAND gate
  74HC08 AND: QUADRUPLE 2-INPUT AND GATES
  74HC32 OR: QUADRUPLE 2-INPUT OR GATES
  74HC04 NOT: SNx4HC04 Hex Inverters SN54HC04, SN74HC04
  74LS02P NOR: (74HC02; 74HCT02 ) Quad 2-input NOR gate HD74LS02
  74HC86 XOR: QUADRUPLE 2-INPUT OR GATES
