// Logisim project ula_8bits.circ as structural Verilog: 14 circuits, main circuit SOMADORCOMPLETO
module ULA (
  input  Bneg,
  input  [2:0] OP,
  input  [7:0] A,
  input  [7:0] B,
  output [7:0] S
);

  wire [7:0] AND_out, c2_1_c2, c2_1_not, equal_1_s, mux_2x1_1_s, OR_out, slt_1_s, somador_1_s, subtrator_1_s;

  MUX_2X1 mux_2x1_1 (.A(B), .B(c2_1_c2), .OP(Bneg), .S(mux_2x1_1_s));
  C2 c2_1 (.B(B), .NOT(c2_1_not), .C2(c2_1_c2));
  SOMADOR somador_1 (.A(A), .B(mux_2x1_1_s), .S(somador_1_s));  // open: OVERFLOW
  SUBTRATOR subtrator_1 (.A(A), .B(mux_2x1_1_s), .S(subtrator_1_s));  // open: overflow
  assign AND_out = A & mux_2x1_1_s;  // AND_Gate AND, 8 bits wide
  assign OR_out = A | mux_2x1_1_s;  // OR_Gate OR, 8 bits wide
  SLT slt_1 (.A(A), .B(mux_2x1_1_s), .S(slt_1_s));
  EQUAL equal_1 (.A(A), .B(mux_2x1_1_s), .S(equal_1_s));
  MUX_8x1 mux_8x1_1 (
    .A(somador_1_s), .B(subtrator_1_s), .C(AND_out), .D(OR_out), .E(slt_1_s), .F(equal_1_s), .G(c2_1_not),
    .H({8{1'b0}}), .OP(OP), .S(S));
endmodule

// +
module SOMADOR (
  input  [7:0] A,
  input  [7:0] B,
  output OVERFLOW,
  output [7:0] S
);

  wire meiosomador_1_vai_1, somadorcompleto_2_vai_1, somadorcompleto_3_vai_1, somadorcompleto_4_vai_1,
       somadorcompleto_5_vai_1, somadorcompleto_6_vai_1, somadorcompleto_7_vai_1;

  SOMADORCOMPLETO somadorcompleto_1 (.A(A[7]), .B(B[7]), .VAI_1(OVERFLOW), .VEM1(somadorcompleto_2_vai_1), .S(S[7]));
  SOMADORCOMPLETO somadorcompleto_2 (
    .A(A[6]), .B(B[6]), .VAI_1(somadorcompleto_2_vai_1), .VEM1(somadorcompleto_3_vai_1), .S(S[6]));
  SOMADORCOMPLETO somadorcompleto_3 (
    .A(A[5]), .B(B[5]), .VAI_1(somadorcompleto_3_vai_1), .VEM1(somadorcompleto_4_vai_1), .S(S[5]));
  SOMADORCOMPLETO somadorcompleto_4 (
    .A(A[4]), .B(B[4]), .VAI_1(somadorcompleto_4_vai_1), .VEM1(somadorcompleto_5_vai_1), .S(S[4]));
  SOMADORCOMPLETO somadorcompleto_5 (
    .A(A[3]), .B(B[3]), .VAI_1(somadorcompleto_5_vai_1), .VEM1(somadorcompleto_6_vai_1), .S(S[3]));
  SOMADORCOMPLETO somadorcompleto_6 (
    .A(A[2]), .B(B[2]), .VAI_1(somadorcompleto_6_vai_1), .VEM1(somadorcompleto_7_vai_1), .S(S[2]));
  SOMADORCOMPLETO somadorcompleto_7 (
    .A(A[1]), .B(B[1]), .VAI_1(somadorcompleto_7_vai_1), .VEM1(meiosomador_1_vai_1), .S(S[1]));
  MEIOSOMADOR meiosomador_1 (.A(A[0]), .B(B[0]), .VAI_1(meiosomador_1_vai_1), .S(S[0]));
endmodule

// SUB
module SUBTRATOR (
  input  [7:0] A,
  input  [7:0] B,
  output overflow,
  output [7:0] S
);

  wire n1_2_sub_1_vai_1, sub_c_2_vai_1, sub_c_3_vai_1, sub_c_4_vai_1, sub_c_5_vai_1, sub_c_6_vai_1,
       sub_c_7_vai_1;

  _1_2_Sub u_1_2_sub_1 (.A(A[0]), .B(B[0]), .Sub(S[0]), .Vai_1(n1_2_sub_1_vai_1));
  Sub_C sub_c_1 (.A(A[7]), .B(B[7]), .Vai_1(overflow), .Vem_1(sub_c_2_vai_1), .Sub(S[7]));
  Sub_C sub_c_2 (.A(A[6]), .B(B[6]), .Vai_1(sub_c_2_vai_1), .Vem_1(sub_c_3_vai_1), .Sub(S[6]));
  Sub_C sub_c_3 (.A(A[5]), .B(B[5]), .Vai_1(sub_c_3_vai_1), .Vem_1(sub_c_4_vai_1), .Sub(S[5]));
  Sub_C sub_c_4 (.A(A[4]), .B(B[4]), .Vai_1(sub_c_4_vai_1), .Vem_1(sub_c_5_vai_1), .Sub(S[4]));
  Sub_C sub_c_5 (.A(A[3]), .B(B[3]), .Vai_1(sub_c_5_vai_1), .Vem_1(sub_c_6_vai_1), .Sub(S[3]));
  Sub_C sub_c_6 (.A(A[2]), .B(B[2]), .Vai_1(sub_c_6_vai_1), .Vem_1(sub_c_7_vai_1), .Sub(S[2]));
  Sub_C sub_c_7 (.A(A[1]), .B(B[1]), .Vai_1(sub_c_7_vai_1), .Vem_1(n1_2_sub_1_vai_1), .Sub(S[1]));
endmodule

module C2 (
  input  [7:0] B,
  output [7:0] C2,
  output [7:0] NOT
);

  wire meiosomador_1_vai_1, not_2_out, somadorcompleto_2_vai_1, somadorcompleto_3_vai_1,
       somadorcompleto_4_vai_1, somadorcompleto_5_vai_1, somadorcompleto_6_vai_1, somadorcompleto_7_vai_1;

  assign NOT = ~B;  // NOT_Gate not_1, 8 bits wide
  not not_2 (not_2_out, 1'b1);
  SOMADORCOMPLETO somadorcompleto_1 (
    .A(NOT[7]), .B(not_2_out), .VEM1(somadorcompleto_2_vai_1), .S(C2[7]));  // open: VAI_1
  SOMADORCOMPLETO somadorcompleto_2 (
    .A(NOT[6]), .B(not_2_out), .VAI_1(somadorcompleto_2_vai_1), .VEM1(somadorcompleto_3_vai_1), .S(C2[6]));
  SOMADORCOMPLETO somadorcompleto_3 (
    .A(NOT[5]), .B(not_2_out), .VAI_1(somadorcompleto_3_vai_1), .VEM1(somadorcompleto_4_vai_1), .S(C2[5]));
  SOMADORCOMPLETO somadorcompleto_4 (
    .A(NOT[4]), .B(not_2_out), .VAI_1(somadorcompleto_4_vai_1), .VEM1(somadorcompleto_5_vai_1), .S(C2[4]));
  SOMADORCOMPLETO somadorcompleto_5 (
    .A(NOT[3]), .B(not_2_out), .VAI_1(somadorcompleto_5_vai_1), .VEM1(somadorcompleto_6_vai_1), .S(C2[3]));
  SOMADORCOMPLETO somadorcompleto_6 (
    .A(NOT[2]), .B(not_2_out), .VAI_1(somadorcompleto_6_vai_1), .VEM1(somadorcompleto_7_vai_1), .S(C2[2]));
  SOMADORCOMPLETO somadorcompleto_7 (
    .A(NOT[1]), .B(not_2_out), .VAI_1(somadorcompleto_7_vai_1), .VEM1(meiosomador_1_vai_1), .S(C2[1]));
  MEIOSOMADOR meiosomador_1 (.A(NOT[0]), .B(1'b1), .VAI_1(meiosomador_1_vai_1), .S(C2[0]));
endmodule

// EQ
module EQUAL (
  input  [7:0] A,
  input  [7:0] B,
  output [7:0] S
);

  wire xnor_1_out, xnor_2_out, xnor_3_out, xnor_4_out, xnor_5_out, xnor_6_out, xnor_7_out, xnor_8_out;

  xnor xnor_1 (xnor_1_out, A[0], B[0]);
  xnor xnor_2 (xnor_2_out, A[1], B[1]);
  xnor xnor_3 (xnor_3_out, A[2], B[2]);
  xnor xnor_4 (xnor_4_out, A[3], B[3]);
  xnor xnor_5 (xnor_5_out, A[4], B[4]);
  xnor xnor_6 (xnor_6_out, A[5], B[5]);
  xnor xnor_7 (xnor_7_out, A[6], B[6]);
  xnor xnor_8 (xnor_8_out, A[7], B[7]);
  and and_1 (S[7], xnor_1_out, xnor_2_out, xnor_3_out, xnor_4_out, xnor_5_out, xnor_6_out, xnor_7_out, xnor_8_out);

  assign S[6:0] = {7{S[7]}};
endmodule

module SLT (
  input  [7:0] A,
  input  [7:0] B,
  output [7:0] S
);

  wire [1:0] slt_2_bits_1_s, slt_2_bits_2_s, slt_2_bits_3_s, slt_2_bits_4_s;

  SLT_2_bits slt_2_bits_1 (.A(A[1:0]), .B(B[1:0]), .S(slt_2_bits_1_s));
  SLT_2_bits slt_2_bits_2 (.A(A[3:2]), .B(B[3:2]), .S(slt_2_bits_2_s));
  SLT_2_bits slt_2_bits_3 (.A(A[5:4]), .B(B[5:4]), .S(slt_2_bits_3_s));
  SLT_2_bits slt_2_bits_4 (.A(A[7:6]), .B(B[7:6]), .S(slt_2_bits_4_s));
  or or_1 (S[7], slt_2_bits_1_s[0], slt_2_bits_1_s[1], slt_2_bits_2_s[0], slt_2_bits_2_s[1], slt_2_bits_3_s[0], slt_2_bits_3_s[1], slt_2_bits_4_s[0], slt_2_bits_4_s[1]);

  assign S[6:0] = {7{S[7]}};
endmodule

// slt2b
module SLT_2_bits (
  input  [1:0] A,
  input  [1:0] B,
  output [1:0] S
);

  wire and_1_out, and_2_out, and_3_out;

  and and_1 (and_1_out, ~A[1], B[1]);  // AND_Gate
  and and_2 (and_2_out, ~A[1], ~A[0], B[0]);  // AND_Gate
  and and_3 (and_3_out, ~A[0], B[1], B[0]);  // AND_Gate
  or or_1 (S[1], and_1_out, and_2_out, and_3_out);

  assign S[0] = S[1];
endmodule

module SUBTATORCOMPLETO (
  input  Vem_1,
  input  A,
  input  B,
  output Sub,
  output Vai_1
);

  wire and_1_out, and_2_out, not_1_out, or_1_out;

  ExactlyOne xor_1 (.out(Sub), .in0(A), .in1(B), .in2(Vem_1));
  or or_1 (or_1_out, B, Vem_1);
  and and_1 (and_1_out, B, Vem_1);
  not not_1 (not_1_out, A);
  and and_2 (and_2_out, or_1_out, not_1_out);
  or or_2 (Vai_1, and_2_out, and_1_out);
endmodule

module MEIOSUBTRATOR (
  input  A,
  input  B,
  output Sub,
  output Vai_1
);

  wire not_1_out;

  not not_1 (not_1_out, A);
  xor xor_1 (Sub, A, B);
  and and_1 (Vai_1, not_1_out, B);
endmodule

// SUM
module SOMADORCOMPLETO (
  input  A,
  input  B,
  input  VEM1,
  output S,
  output VAI_1
);

  wire and_1_out, and_2_out, and_3_out, xor_1_out;

  xor xor_1 (xor_1_out, A, B);
  and and_1 (and_1_out, A, B);
  and and_2 (and_2_out, A, VEM1);
  and and_3 (and_3_out, B, VEM1);
  xor xor_2 (S, xor_1_out, VEM1);
  or or_1 (VAI_1, and_1_out, and_2_out, and_3_out);
endmodule

// 1/2
module MEIOSOMADOR (
  input  A,
  input  B,
  output S,
  output VAI_1
);

  xor xor_1 (S, A, B);
  and and_1 (VAI_1, A, B);
endmodule

// MUX
module MUX_2X1 (
  input  OP,
  input  [7:0] A,
  input  [7:0] B,
  output [7:0] S
);

  wire and_1_out, and_2_out, and_3_out, and_4_out, and_5_out, and_6_out, and_7_out, and_8_out, and_9_out,
       and_10_out, and_11_out, and_12_out, and_13_out, and_14_out, and_15_out, and_16_out;

  and and_1 (and_1_out, A[7], ~OP);  // AND_Gate
  and and_2 (and_2_out, B[7], OP);
  and and_3 (and_3_out, A[6], ~OP);  // AND_Gate
  and and_4 (and_4_out, B[6], OP);
  and and_5 (and_5_out, A[5], ~OP);  // AND_Gate
  and and_6 (and_6_out, B[5], OP);
  and and_7 (and_7_out, A[4], ~OP);  // AND_Gate
  and and_8 (and_8_out, B[4], OP);
  and and_9 (and_9_out, A[3], ~OP);  // AND_Gate
  and and_10 (and_10_out, B[3], OP);
  and and_11 (and_11_out, A[2], ~OP);  // AND_Gate
  and and_12 (and_12_out, B[2], OP);
  and and_13 (and_13_out, A[1], ~OP);  // AND_Gate
  and and_14 (and_14_out, B[1], OP);
  and and_15 (and_15_out, A[0], ~OP);  // AND_Gate
  and and_16 (and_16_out, B[0], OP);
  or or_1 (S[7], and_1_out, and_2_out);
  or or_2 (S[6], and_3_out, and_4_out);
  or or_3 (S[5], and_5_out, and_6_out);
  or or_4 (S[4], and_7_out, and_8_out);
  or or_5 (S[3], and_9_out, and_10_out);
  or or_6 (S[2], and_11_out, and_12_out);
  or or_7 (S[1], and_13_out, and_14_out);
  or or_8 (S[0], and_15_out, and_16_out);
endmodule

// MUX
module MUX_4X1 (
  input  [1:0] in_1,
  input  [7:0] A,
  input  [7:0] B,
  input  [7:0] C,
  input  [7:0] D,
  output [7:0] out_6
);

  wire [7:0] mux_2x1_1_s, mux_2x1_3_s;

  MUX_2X1 mux_2x1_1 (.A(A), .B(B), .OP(in_1[0]), .S(mux_2x1_1_s));
  MUX_2X1 mux_2x1_2 (.A(mux_2x1_1_s), .B(mux_2x1_3_s), .OP(in_1[1]), .S(out_6));
  MUX_2X1 mux_2x1_3 (.A(C), .B(D), .OP(in_1[0]), .S(mux_2x1_3_s));
endmodule

// MUX
module MUX_8x1 (
  input  [2:0] OP,
  input  [7:0] A,
  input  [7:0] B,
  input  [7:0] C,
  input  [7:0] D,
  input  [7:0] E,
  input  [7:0] F,
  input  [7:0] G,
  input  [7:0] H,
  output [7:0] S
);

  wire [7:0] mux_4x1_1_out_6, mux_4x1_2_out_6;

  MUX_4X1 mux_4x1_1 (.A(A), .B(B), .C(C), .D(D), .in_1(OP[1:0]), .out_6(mux_4x1_1_out_6));
  MUX_4X1 mux_4x1_2 (.A(E), .B(F), .C(G), .D(H), .in_1(OP[1:0]), .out_6(mux_4x1_2_out_6));
  MUX_2X1 mux_2x1_1 (.A(mux_4x1_1_out_6), .B(mux_4x1_2_out_6), .OP(OP[2]), .S(S));
endmodule
